// Logisim project Branch Control.circ as structural Verilog: 1 circuit, main circuit Branch Control
module Branch_Control (
  input  [31:0] RS,
  input  [31:0] PC,
  input  [25:0] Destiny,
  input  [15:0] Offset,
  input  [2:0] Operation,
  input  ZF,
  input  NF,
  output [31:0] PC_prime
);

  wire and_1_out, and_2_out, and_3_out, and_4_out, and_5_out, beq, bgtz, blez, bltz, bne, branch,
       comparator_1_eq, comparator_1_lt, jr, nop, RS__0;
  wire [1:0] Select;
  wire [31:0] Branch_Amount, multiplier_1_out, Regular;
  wire [31:28] J_Jump;

  Comparator #(.width(32)) comparator_1 (
    .a(RS), .b({32{1'b0}}), .eq(comparator_1_eq), .lt(comparator_1_lt));  // open: gt
  or or_1 (RS__0, comparator_1_eq, comparator_1_lt);
  Decoder #(.select(3), .enable("false")) decoder_1 (
    .out0(nop), .out1(beq), .out2(bne), .out3(blez), .out4(bgtz), .out5(bltz), .out6(branch), .out7(jr),
    .sel(Operation));
  Adder #(.width(32)) adder_1 (.a(PC), .b(32'h4), .out(Regular));  // open: cin, cout
  Multiplier #(.width(32)) multiplier_1 (.a(32'h4), .b(RS), .out(multiplier_1_out));  // open: cin, cout
  Priority_Encoder #(.select(2)) priority_encoder_1 (
    .in0(1'b1), .in1(branch), .in2(branch), .in3(jr), .out(Select), .en_in(1'b1));  // open: gs, en_out
  Adder #(.width(32)) adder_2 (.a(Regular), .b(multiplier_1_out), .out(Branch_Amount));  // open: cin, cout
  and and_1 (and_1_out, beq, ZF);
  and and_2 (and_2_out, bne, ~ZF);  // AND_Gate
  and and_3 (and_3_out, blez, RS__0);
  and and_4 (and_4_out, bgtz, ~RS__0);  // AND_Gate
  and and_5 (and_5_out, bltz, NF);
  BitSelector #(.width(32), .group(4)) bitselector_1 (.in(PC), .out(J_Jump), .sel(3'b111));
  or or_2 (branch, and_1_out, and_2_out, and_3_out, and_4_out, and_5_out);
  Multiplexer #(.select(2), .width(32), .enable("false")) multiplexer_1 (
    .in0(Regular), .in1(Branch_Amount), .in2({J_Jump, Destiny, 2'b00}), .in3(RS), .out(PC_prime), .sel(Select));

  // Other names for the same wires on the sheet: j = branch; J_Jump[27:2] = Destiny; Op[2:0] = Operation

  // Notes on the sheet:
  //   Inputs
  //   Operations
  //   Selection Process
  //   PC Transformation
  //   I-Instructions
  //   Outputs
endmodule
