// Logisim project Cache Memory.circ as structural Verilog: 1 circuit, main circuit main
module main (
  input  [31:0] RAM_In_0,
  input  Clk,
  input  Rst,
  input  R_W,
  input  [31:0] RAM_In_1,
  input  Find,
  input  [3:0] RT,
  input  [31:0] RAM_In_2,
  input  [31:0] RAM_In_3,
  input  [31:0] Address,
  output [31:0] Instruction,
  output [15:0] RAM_Address,
  output [1:0] Offset,
  output HIT
);

  wire and_1_out, and_3_out, and_4_out, comparator_1_eq, comparator_2_eq, d_ff_1_q, En_0, En_1, En_2, En_3,
       nor_1_out, or_1_out, Ready_RT, V_0, V_1, V_2, V_3, Validated;
  wire [3:0] counter_1_q, subtractor_1_out;
  wire [13:0] Selected_Tag, Tag_0, Tag_1, Tag_3;
  wire [31:0] multiplexer_1_out, multiplexer_2_out, multiplexer_4_out, multiplexer_5_out, Out_0, Out_1,
       Out_2, Out_3, Out_4, Out_5, Out_6, Out_7, Out_8, Out_9, Out_10, Out_11, Out_12, Out_13, Out_14, Out_15;

  Register #(.width(14)) register_1 (.D(Address[19:6]), .en(En_0), .Q(Tag_0), .clk(Clk), .clr(Rst));
  Register #(.width(14)) register_2 (.D(Address[19:6]), .en(En_1), .Q(Tag_1), .clk(Clk), .clr(Rst));
  Register #(.width(14)) register_3 (.D(Address[19:6]), .en(En_2), .Q(Tag_1), .clk(Clk), .clr(Rst));
  Register #(.width(14)) register_4 (.D(Address[19:6]), .en(En_3), .Q(Tag_3), .clk(Clk), .clr(Rst));
  Multiplexer #(.select(2), .width(32), .enable("false")) multiplexer_1 (
    .in0(Out_0), .in1(Out_4), .in2(Out_8), .in3(Out_12), .out(multiplexer_1_out), .sel(Address[5:4]));
  Multiplexer #(.select(2), .width(32), .enable("false")) multiplexer_2 (
    .in0(Out_3), .in1(Out_7), .in2(Out_11), .in3(Out_15), .out(multiplexer_2_out), .sel(Address[5:4]));
  Multiplexer #(.select(2), .width(14), .enable("false")) multiplexer_3 (
    .in0(Tag_0), .in1(Tag_1), .in2(Tag_1), .in3(Tag_3), .out(Selected_Tag), .sel(Address[5:4]));
  Multiplexer #(.select(2), .width(32), .enable("false")) multiplexer_4 (
    .in0(Out_1), .in1(Out_5), .in2(Out_9), .in3(Out_13), .out(multiplexer_4_out), .sel(Address[5:4]));
  Multiplexer #(.select(2), .width(32), .enable("false")) multiplexer_5 (
    .in0(Out_2), .in1(Out_6), .in2(Out_10), .in3(Out_14), .out(multiplexer_5_out), .sel(Address[5:4]));
  Register #(.width(32)) register_5 (.D(RAM_In_0), .en(En_0), .Q(Out_0), .clk(Clk), .clr(Rst));
  Register #(.width(32)) register_6 (.D(RAM_In_0), .en(En_1), .Q(Out_4), .clk(Clk), .clr(Rst));
  Register #(.width(32)) register_7 (.D(RAM_In_0), .en(En_2), .Q(Out_8), .clk(Clk), .clr(Rst));
  Register #(.width(32)) register_8 (.D(RAM_In_0), .en(En_3), .Q(Out_12), .clk(Clk), .clr(Rst));
  Multiplexer #(.select(2), .enable("false")) multiplexer_6 (
    .in0(V_0), .in1(V_1), .in2(V_2), .in3(V_3), .out(Validated), .sel(Address[5:4]));
  Multiplexer #(.select(2), .width(32), .enable("false")) multiplexer_7 (
    .in0(multiplexer_1_out), .in1(multiplexer_4_out), .in2(multiplexer_5_out), .in3(multiplexer_2_out),
    .out({Instruction[7:0], Instruction[15:8], Instruction[23:16], Instruction[31:24]}), .sel(Address[3:2]));
  Register #(.width(32)) register_9 (.D(RAM_In_1), .en(En_0), .Q(Out_1), .clk(Clk), .clr(Rst));
  Register #(.width(32)) register_10 (.D(RAM_In_1), .en(En_1), .Q(Out_5), .clk(Clk), .clr(Rst));
  Register #(.width(32)) register_11 (.D(RAM_In_1), .en(En_2), .Q(Out_9), .clk(Clk), .clr(Rst));
  Register #(.width(32)) register_12 (.D(RAM_In_1), .en(En_3), .Q(Out_13), .clk(Clk), .clr(Rst));
  Register #(.width(32)) register_13 (.D(RAM_In_2), .en(En_0), .Q(Out_2), .clk(Clk), .clr(Rst));
  Register #(.width(32)) register_14 (.D(RAM_In_2), .en(En_1), .Q(Out_6), .clk(Clk), .clr(Rst));
  Register #(.width(32)) register_15 (.D(RAM_In_2), .en(En_2), .Q(Out_10), .clk(Clk), .clr(Rst));
  Register #(.width(32)) register_16 (.D(RAM_In_2), .en(En_3), .Q(Out_14), .clk(Clk), .clr(Rst));
  and and_1 (and_1_out, ~R_W, Find, ~HIT);  // AND_Gate
  Register #(.width(32)) register_17 (.D(RAM_In_3), .en(En_0), .Q(Out_3), .clk(Clk), .clr(Rst));
  Register #(.width(32)) register_18 (.D(RAM_In_3), .en(En_1), .Q(Out_7), .clk(Clk), .clr(Rst));
  Register #(.width(32)) register_19 (.D(RAM_In_3), .en(En_2), .Q(Out_11), .clk(Clk), .clr(Rst));
  Register #(.width(32)) register_20 (.D(RAM_In_3), .en(En_3), .Q(Out_15), .clk(Clk), .clr(Rst));
  Comparator #(.width(14)) comparator_1 (.a(Selected_Tag), .b(Address[19:6]), .eq(comparator_1_eq));  // open: gt, lt
  and and_2 (HIT, comparator_1_eq, Ready_RT);
  and and_3 (and_3_out, and_1_out, ~Ready_RT);  // AND_Gate
  Subtractor #(.width(4)) subtractor_1 (.a(RT), .b(4'b0001), .out(subtractor_1_out));  // open: bin, bout
  D_Flip_Flop d_ff_1 (.clk(Clk), .D(and_3_out), .Q(d_ff_1_q), .reset(Rst));  // open: Qn, preset, en
  Counter #(.width(4), .max('hf)) counter_1 (
    .load(and_1_out), .D(subtractor_1_out), .count(d_ff_1_q), .Q(counter_1_q), .clk(Clk), .clr(Rst));  // open: carry
  D_Flip_Flop d_ff_2 (.clk(Clk), .D(Ready_RT), .Q(V_0), .en(En_0), .reset(Rst));  // open: Qn, preset
  D_Flip_Flop d_ff_3 (.clk(Clk), .D(Ready_RT), .Q(V_1), .en(En_1), .reset(Rst));  // open: Qn, preset
  D_Flip_Flop d_ff_4 (.clk(Clk), .D(Ready_RT), .Q(V_2), .en(En_2), .reset(Rst));  // open: Qn, preset
  D_Flip_Flop d_ff_5 (.clk(Clk), .D(Ready_RT), .Q(V_3), .en(En_3), .reset(Rst));  // open: Qn, preset
  Demultiplexer #(.select(2), .enable("false")) demultiplexer_1 (
    .out0(En_0), .out1(En_1), .out2(En_2), .out3(En_3), .in(or_1_out), .sel(Address[5:4]));
  or or_1 (or_1_out, Ready_RT, R_W);
  nor nor_1 (nor_1_out, counter_1_q[0], counter_1_q[1], counter_1_q[2], counter_1_q[3]);
  and and_4 (and_4_out, nor_1_out, d_ff_1_q);
  Comparator #(.width(4)) comparator_2 (.a(RT), .b(4'b0000), .eq(comparator_2_eq));  // open: gt, lt
  or or_2 (Ready_RT, and_4_out, comparator_2_eq);

  assign Offset = Address[3:2];
  assign RAM_Address = Address[19:4];

  // Other names for the same wires on the sheet: Index[1:0] = Address[5:4]; R_Address[15:0] = Address[19:4];
  //   Tag[13:0] = Address[19:6]; In_0[31:0] = RAM_In_0; In_1[31:0] = RAM_In_1; In_2[31:0] = RAM_In_2;
  //   In_3[31:0] = RAM_In_3; Tag_2[13:0] = Tag_1; Validate = Ready_RT

  // Notes on the sheet:
  //   Inputs
  //   Tags
  //   Search Process
  //   Set Instruction
  //   Memory
  //   Validate
  //   RT Waiting Process
  //   Outputs
endmodule
