// Logisim project Instruction Decoder.circ as structural Verilog: 1 circuit, main circuit main
module main (
  input  [31:0] Instruction,
  input  Load_Instruction,
  input  Clock,
  input  Reset,
  output [4:0] Data_Address,
  output [25:0] Address,
  output [4:0] Selector_A,
  output [4:0] Selector_B,
  output [5:0] Operation_Code,
  output [15:0] Offset,
  output [5:0] Function_Code
);

  Register #(.width(32)) Current_Instruction (
    .D(Instruction), .en(Load_Instruction), .Q({Operation_Code, Address}), .clk(Clock), .clr(Reset));

  assign Data_Address = Address[15:11];
  assign Function_Code = Address[5:0];
  assign Offset = Address[15:0];
  assign Selector_A = Address[25:21];
  assign Selector_B = Address[20:16];

  // Other names for the same wires on the sheet: Immediate[15:0] = Address[15:0]; Rd[4:0] = Address[15:11];
  //   Rt[4:0] = Address[20:16]; Rs[4:0] = Address[25:21]; clk = Clock; Instuc[31:0] = Instruction;
  //   Load_Instuc = Load_Instruction; res = Reset

  // Notes on the sheet:
  //   INPUT ZONE
  //   OUTPUT ZONE
endmodule
