// Logisim project Operation Decoder.circ as structural Verilog: 1 circuit, main circuit Operation Decoder
module Operation_Decoder (
  input  [5:0] OP_Code,
  input  [5:0] FUNC_Code,
  output [2:0] CU_Op,
  output [2:0] BC_Op,
  output [3:0] ALU_Op,
  output [1:0] B_Select,
  output [2:0] DI_Select,
  output [1:0] Special_Op,
  output Log_Imm_Op,
  output lw,
  output pop
);

  wire add, addi, adds, ALU_OP_t, \and , and_11_out, and_13_out, and_15_out, and_17_out, and_19_out,
       and_21_out, and_29_out, and_31_out, and_32_out, and_33_out, and_34_out, and_35_out, and_36_out,
       and_45_out, and_46_out, and_47_out, and_51_out, and_52_out, and_55_out, and_56_out, and_57_out,
       and_58_out, and_63_out, and_64_out, andi, ands, B_Jump, beq, bgtz, blez, bltz, bne, Branch_OP, div,
       divu, F_000000, halt, Immediate_OP, j, jr, kbd, mfhi, mflo, mult, Mult_Div_OP, mulu, nop, \nor ,
       OP_000000, OP_111000, OP_111111, \or , or_17_out, or_19_out, or_20_out, ori, ors, push, RAM_OP,
       Register_OP, rnd, rt_rd, sliti, slitiu, slt, slts, sltu, sltus, Special_OP_t, Stack_OP, sub, subs, sw,
       tty, \xor , xori, xors;

  // Probe on OP_Code
  // Probe on FUNC_Code
  and and_1 (OP_000000, ~OP_Code[0], ~OP_Code[1], ~OP_Code[2], ~OP_Code[3], ~OP_Code[4], ~OP_Code[5]);  // AND_Gate
  and and_2 (OP_111000, ~OP_Code[0], ~OP_Code[1], ~OP_Code[2], OP_Code[3], OP_Code[4], OP_Code[5]);  // AND_Gate
  and and_3 (OP_111111, OP_Code[0], OP_Code[1], OP_Code[2], OP_Code[3], OP_Code[4], OP_Code[5]);
  and and_4 (F_000000, ~FUNC_Code[0], ~FUNC_Code[1], ~FUNC_Code[2], ~FUNC_Code[3], ~FUNC_Code[4], ~FUNC_Code[5]);  // AND_Gate
  and and_5 (addi, ~OP_Code[0], ~OP_Code[1], ~OP_Code[2], OP_Code[3], ~OP_Code[4], ~OP_Code[5]);  // AND_Gate
  and and_6 (sliti, ~OP_Code[0], OP_Code[1], ~OP_Code[2], OP_Code[3], ~OP_Code[4], ~OP_Code[5]);  // AND_Gate
  and and_7 (slitiu, OP_Code[0], OP_Code[1], ~OP_Code[2], OP_Code[3], ~OP_Code[4], ~OP_Code[5]);  // AND_Gate
  and and_8 (andi, ~OP_Code[0], ~OP_Code[1], OP_Code[2], OP_Code[3], ~OP_Code[4], ~OP_Code[5]);  // AND_Gate
  and and_9 (ori, OP_Code[0], ~OP_Code[1], OP_Code[2], OP_Code[3], ~OP_Code[4], ~OP_Code[5]);  // AND_Gate
  and and_10 (xori, ~OP_Code[0], OP_Code[1], OP_Code[2], OP_Code[3], ~OP_Code[4], ~OP_Code[5]);  // AND_Gate
  and and_11 (and_11_out, ~FUNC_Code[0], ~FUNC_Code[1], ~FUNC_Code[2], ~FUNC_Code[3], ~FUNC_Code[4], FUNC_Code[5]);  // AND_Gate
  and and_12 (add, and_11_out, OP_000000);
  and and_13 (and_13_out, ~FUNC_Code[0], FUNC_Code[1], ~FUNC_Code[2], ~FUNC_Code[3], ~FUNC_Code[4], FUNC_Code[5]);  // AND_Gate
  and and_14 (sub, and_13_out, OP_000000);
  and and_15 (and_15_out, ~FUNC_Code[0], ~FUNC_Code[1], ~FUNC_Code[2], FUNC_Code[3], FUNC_Code[4], ~FUNC_Code[5]);  // AND_Gate
  and and_16 (mult, and_15_out, OP_000000);
  and and_17 (and_17_out, FUNC_Code[0], ~FUNC_Code[1], ~FUNC_Code[2], FUNC_Code[3], FUNC_Code[4], ~FUNC_Code[5]);  // AND_Gate
  and and_18 (mulu, and_17_out, OP_000000);
  and and_19 (and_19_out, ~FUNC_Code[0], FUNC_Code[1], ~FUNC_Code[2], FUNC_Code[3], FUNC_Code[4], ~FUNC_Code[5]);  // AND_Gate
  and and_20 (div, and_19_out, OP_000000);
  and and_21 (and_21_out, FUNC_Code[0], FUNC_Code[1], ~FUNC_Code[2], FUNC_Code[3], FUNC_Code[4], ~FUNC_Code[5]);  // AND_Gate
  and and_22 (divu, and_21_out, OP_000000);
  and and_23 (beq, ~OP_Code[0], ~OP_Code[1], OP_Code[2], ~OP_Code[3], ~OP_Code[4], ~OP_Code[5]);  // AND_Gate
  and and_24 (bne, OP_Code[0], ~OP_Code[1], OP_Code[2], ~OP_Code[3], ~OP_Code[4], ~OP_Code[5]);  // AND_Gate
  and and_25 (blez, ~OP_Code[0], OP_Code[1], OP_Code[2], ~OP_Code[3], ~OP_Code[4], ~OP_Code[5]);  // AND_Gate
  and and_26 (bgtz, OP_Code[0], OP_Code[1], OP_Code[2], ~OP_Code[3], ~OP_Code[4], ~OP_Code[5]);  // AND_Gate
  and and_27 (bltz, OP_Code[0], ~OP_Code[1], ~OP_Code[2], ~OP_Code[3], ~OP_Code[4], ~OP_Code[5]);  // AND_Gate
  and and_28 (j, ~OP_Code[0], OP_Code[1], ~OP_Code[2], ~OP_Code[3], ~OP_Code[4], ~OP_Code[5]);  // AND_Gate
  and and_29 (and_29_out, ~OP_Code[0], ~OP_Code[1], ~OP_Code[2], ~OP_Code[3], ~OP_Code[4], ~OP_Code[5]);  // AND_Gate
  and and_30 (nop, and_29_out, F_000000);
  and and_31 (and_31_out, ~FUNC_Code[0], ~FUNC_Code[1], FUNC_Code[2], ~FUNC_Code[3], ~FUNC_Code[4], FUNC_Code[5]);  // AND_Gate
  and and_32 (and_32_out, FUNC_Code[0], ~FUNC_Code[1], FUNC_Code[2], ~FUNC_Code[3], ~FUNC_Code[4], FUNC_Code[5]);  // AND_Gate
  and and_33 (and_33_out, FUNC_Code[0], FUNC_Code[1], FUNC_Code[2], ~FUNC_Code[3], ~FUNC_Code[4], FUNC_Code[5]);  // AND_Gate
  and and_34 (and_34_out, ~FUNC_Code[0], ~FUNC_Code[1], ~FUNC_Code[2], FUNC_Code[3], ~FUNC_Code[4], FUNC_Code[5]);  // AND_Gate
  and and_35 (and_35_out, ~FUNC_Code[0], FUNC_Code[1], ~FUNC_Code[2], FUNC_Code[3], ~FUNC_Code[4], FUNC_Code[5]);  // AND_Gate
  and and_36 (and_36_out, FUNC_Code[0], FUNC_Code[1], ~FUNC_Code[2], FUNC_Code[3], ~FUNC_Code[4], FUNC_Code[5]);  // AND_Gate
  and and_37 (\and , and_31_out, OP_000000);
  and and_38 (\or , and_32_out, OP_000000);
  and and_39 (\nor , and_33_out, OP_000000);
  and and_40 (\xor , and_34_out, OP_000000);
  and and_41 (slt, and_35_out, OP_000000);
  and and_42 (sltu, and_36_out, OP_000000);
  and and_43 (lw, OP_Code[0], OP_Code[1], ~OP_Code[2], ~OP_Code[3], ~OP_Code[4], OP_Code[5]);  // AND_Gate
  and and_44 (sw, OP_Code[0], OP_Code[1], ~OP_Code[2], OP_Code[3], ~OP_Code[4], OP_Code[5]);  // AND_Gate
  and and_45 (and_45_out, ~FUNC_Code[0], ~FUNC_Code[1], ~FUNC_Code[2], FUNC_Code[3], ~FUNC_Code[4], ~FUNC_Code[5]);  // AND_Gate
  and and_46 (and_46_out, ~FUNC_Code[0], ~FUNC_Code[1], ~FUNC_Code[2], ~FUNC_Code[3], FUNC_Code[4], ~FUNC_Code[5]);  // AND_Gate
  and and_47 (and_47_out, ~FUNC_Code[0], FUNC_Code[1], ~FUNC_Code[2], ~FUNC_Code[3], FUNC_Code[4], ~FUNC_Code[5]);  // AND_Gate
  or or_1 (ALU_OP_t, add, sub, mult, mulu, div, divu, slt, sltu, \and , \or , \nor , \xor );
  or or_2 (Branch_OP, nop, beq, bne, blez, bgtz, bltz, j, jr);
  or or_3 (Immediate_OP, addi, sliti, slitiu, andi, ori, xori);
  or or_4 (Log_Imm_Op, andi, ori, xori);
  and and_48 (jr, and_45_out, OP_000000);
  and and_49 (mfhi, and_46_out, OP_000000);
  and and_50 (mflo, and_47_out, OP_000000);
  or or_5 (Special_OP_t, halt, rnd, kbd, tty);
  or or_6 (Stack_OP, pop, push);
  or or_7 (RAM_OP, lw, sw);
  or or_8 (Register_OP, mfhi, mflo);
  or or_9 (Mult_Div_OP, mult, mulu, div, divu);
  and and_51 (and_51_out, ~FUNC_Code[0], ~FUNC_Code[1], ~FUNC_Code[2], ~FUNC_Code[3], ~FUNC_Code[4], ~FUNC_Code[5]);  // AND_Gate
  and and_52 (and_52_out, FUNC_Code[0], ~FUNC_Code[1], ~FUNC_Code[2], ~FUNC_Code[3], ~FUNC_Code[4], ~FUNC_Code[5]);  // AND_Gate
  and and_53 (pop, and_51_out, OP_111000);
  and and_54 (push, and_52_out, OP_111000);
  and and_55 (and_55_out, FUNC_Code[0], FUNC_Code[1], FUNC_Code[2], FUNC_Code[3], FUNC_Code[4], FUNC_Code[5]);
  and and_56 (and_56_out, ~FUNC_Code[0], FUNC_Code[1], ~FUNC_Code[2], ~FUNC_Code[3], ~FUNC_Code[4], ~FUNC_Code[5]);  // AND_Gate
  and and_57 (and_57_out, ~FUNC_Code[0], ~FUNC_Code[1], FUNC_Code[2], ~FUNC_Code[3], ~FUNC_Code[4], ~FUNC_Code[5]);  // AND_Gate
  and and_58 (and_58_out, FUNC_Code[0], ~FUNC_Code[1], ~FUNC_Code[2], ~FUNC_Code[3], ~FUNC_Code[4], ~FUNC_Code[5]);  // AND_Gate
  and and_59 (halt, and_55_out, OP_111111);
  and and_60 (rnd, and_56_out, OP_111111);
  and and_61 (kbd, and_57_out, OP_111111);
  and and_62 (tty, and_58_out, OP_111111);
  or or_10 (adds, add, RAM_OP, addi);
  or or_11 (subs, sub, B_Jump);
  or or_12 (ands, \and , andi);
  or or_13 (ors, \or , ori);
  or or_14 (xors, \xor , xori);
  or or_15 (slts, slt, sliti);
  or or_16 (sltus, sltu, slitiu);
  or or_17 (or_17_out, halt, 1'b1);
  Priority_Encoder priority_encoder_1 (
    .in0(1'b1), .in1(beq), .in2(bne), .in3(blez), .in4(bgtz), .in5(bltz), .in6(j), .in7(jr), .out(BC_Op),
    .en_in(1'b1));  // open: gs, en_out
  or or_18 (B_Jump, beq, bne, blez, bgtz, bltz);
  Priority_Encoder #(.select(2)) priority_encoder_2 (
    .in0(or_17_out), .in1(rnd), .in2(kbd), .in3(tty), .out(Special_Op), .en_in(1'b1));  // open: gs, en_out
  Priority_Encoder #(.disabled(0)) priority_encoder_3 (
    .in0(Branch_OP), .in1(ALU_OP_t), .in2(Immediate_OP), .in3(Register_OP), .in4(RAM_OP), .in5(Stack_OP),
    .in6(Special_OP_t), .out(CU_Op), .en_in(1'b1));  // open: in7, gs, en_out
  or or_19 (or_19_out, blez, bgtz, bltz);
  or or_20 (or_20_out, RAM_OP, Immediate_OP);
  and and_63 (and_63_out, lw, pop);
  and and_64 (and_64_out, ~B_Jump, ~RAM_OP, ~Immediate_OP, ~ALU_OP_t);  // AND_Gate
  or or_21 (rt_rd, OP_000000, OP_111000, OP_111111);
  Priority_Encoder #(.select(4)) priority_encoder_4 (
    .in0(adds), .in1(subs), .in2(ands), .in3(ors), .in4(\nor ), .in5(xors), .in6(slts), .in7(sltus),
    .in8(mult), .in9(mulu), .in10(div), .in11(divu), .in15(and_64_out), .out(ALU_Op), .en_in(1'b1));  // open: in12, in13, in14, gs, en_out
  Priority_Encoder #(.select(2)) priority_encoder_5 (
    .in0(1'b1), .in1(or_19_out), .in2(or_20_out), .out(B_Select), .en_in(1'b1));  // open: in3, gs, en_out
  Priority_Encoder priority_encoder_6 (
    .in0(1'b1), .in1(and_63_out), .in2(mfhi), .in3(mflo), .in4(kbd), .in5(rnd), .out(DI_Select));  // open: in6, in7, en_in, gs, en_out

  // Other names for the same wires on the sheet: Logical_Immediate_OP = Log_Imm_Op

  // Notes on the sheet:
  //   INPUTS
  //   No Op
  //   TIpo R
  //   Push/Pop
  //   Specials
  //   ALU 
  //   ALU 
  //   Op Code Decode
  //   Branch
  //   RAM
  //   Registers
  //   Func Code Decode
  //   Operations
  //   Stacks
  //   Specials
  //   Ouput
  //   CU
  //   BC
  //   ALU
  //   Specials
  //   Signals
endmodule
