// Logisim project RAM Manager.circ as structural Verilog: 1 circuit, main circuit main
module main (
  input  [31:0] Address_In,
  input  Clk,
  input  Rst,
  input  Save_Data,
  input  [31:0] RAM_00,
  input  [31:0] RAM_01,
  input  [31:0] RAM_In,
  input  [31:0] RAM_02,
  input  [31:0] RAM_03,
  output [15:0] Address_Out,
  output [31:0] RAM_00_2,
  output [31:0] RAM_01_2,
  output [31:0] RAM_Out,
  output [31:0] RAM_02_2,
  output [31:0] RAM_03_2
);

  wire [1:0] Bank;
  wire [3:0] Mask;
  wire [15:2] divider_1_rem;
  wire [31:0] shifter_1_out;

  Shifter #(.width(32), .shift("lr")) shifter_1 (.in(Address_In), .\dist (5'b00010), .out(shifter_1_out));
  Register #(.width(32)) register_1 (
    .D(RAM_In), .en(Save_Data), .Q({RAM_00_2[7:0], RAM_00_2[15:8], RAM_00_2[23:16], RAM_00_2[31:24]}),
    .clk(Clk), .clr(Rst));
  Decoder #(.select(2), .enable("false")) decoder_1 (
    .out0(Mask[0]), .out1(Mask[1]), .out2(Mask[2]), .out3(Mask[3]), .sel(Bank));
  Divider #(.width(16)) divider_1 (
    .a(shifter_1_out[15:0]), .b(16'h4), .out(Address_Out), .rem({divider_1_rem, Bank}));  // open: upper
  Multiplexer #(.select(2), .width(32), .enable("false")) multiplexer_1 (
    .in0(RAM_00), .in1(RAM_01), .in2(RAM_02), .in3(RAM_03),
    .out({RAM_Out[7:0], RAM_Out[15:8], RAM_Out[23:16], RAM_Out[31:24]}), .sel(Bank));

  assign RAM_01_2 = RAM_00_2;
  assign RAM_02_2 = RAM_00_2;
  assign RAM_03_2 = RAM_00_2;
endmodule
