// Logisim project Sign Extender.circ as structural Verilog: 1 circuit, main circuit Sign Extender
module Sign_Extender (
  input  [15:0] Data_In,
  input  Operation,
  output [31:0] Data_Out
);

  wire [31:0] bit_extender_1_out, bit_extender_2_out;

  assign bit_extender_1_out = {{16{Data_In[15]}}, Data_In};  // Bit_Extender bit_extender_1
  assign bit_extender_2_out = {{16{1'b0}}, Data_In};  // Bit_Extender bit_extender_2
  Multiplexer #(.width(32), .enable("false")) multiplexer_1 (
    .in0(bit_extender_1_out), .in1(bit_extender_2_out), .out(Data_Out), .sel(Operation));

  // Other names for the same wires on the sheet: Op = Operation

  // Notes on the sheet:
  //   Inputs
  //   Outputs
endmodule
