// Logisim project s-mips.circ as structural Verilog: 16 circuits, main circuit S-MIPS Board
module S_MIPS_Board (
  input  DESHABILITAR_DISPATCHER,
  output halt
);

  wire button_1_out, CLK, CS, d_ff_1_q, d_ff_1_qn, LCLR, LoadRAM, LoadRAMOn, LW, R_R_W, R_W,
       ram_dispatcher_1_finished, RCS, Reset_out, RST, TTY_EN, undriven, undriven_2;
  wire [2:0] KDB;
  wire [3:0] LMask, Mask, ram_1_read_time, ram_1_write_time, RMask;
  wire [6:0] KDB_DATA, TTY_DATA;
  wire [15:0] Addr, LAddr, RAddr;
  wire [31:0] I0, I1, I2, I3, LData, ram_1_data_out_0, ram_1_data_out_1, ram_1_data_out_2, ram_1_data_out_3,
       RI0, RI1, RI2, RI3;

  TTY #(.rows(25), .cols(80)) tty_1 (.data(TTY_DATA), .clk(CLK), .we(TTY_EN), .clr(RST));
  not not_1 (LoadRAMOn, ram_dispatcher_1_finished);
  RAM_Dispatcher ram_dispatcher_1 (
    .WriteTime(ram_1_write_time), .Clock(CLK), .Data(LData), .Address(LAddr), .Mask(LMask),
    .Finished(ram_dispatcher_1_finished), .Write(LW), .CLR(LCLR));
  Keyboard #(.buflen(64)) keyboard_1 (.clk(CLK), .re(KDB[0]), .clr(KDB[1]), .avail(KDB[2]), .data(KDB_DATA));
  RAM ram_1 (
    .Address(RAddr), .Data_Out_0(ram_1_data_out_0), .Data_Out_1(ram_1_data_out_1),
    .Data_Out_2(ram_1_data_out_2), .Data_Out_3(ram_1_data_out_3), .Data_In_0(RI0), .Data_In_1(RI1),
    .Data_In_2(RI2), .Data_In_3(RI3), .Mask(RMask), .nRead_Write(R_R_W), .Chip_Select(RCS),
    .Read_Time(ram_1_read_time), .Reset(button_1_out), .Write_Time(ram_1_write_time));
  Button button_1 (.out(button_1_out));
  D_Flip_Flop d_ff_1 (
    .clk(CLK), .D(1'b1), .Q(d_ff_1_q), .Qn(d_ff_1_qn), .preset(undriven), .en(undriven_2), .reset(Reset_out));
  D_Flip_Flop d_ff_2 (
    .clk(CLK), .D(1'b1), .Q(d_ff_1_q), .Qn(d_ff_1_qn), .preset(undriven), .en(undriven_2), .reset(Reset_out));
  Button Reset (.out(Reset_out));
  S_MIPS s_mips_1 (
    .Kbd_Enable(KDB[0]), .Address(Addr), .Kbd_Clear(KDB[1]), .Kbd_Available(KDB[2]), .RAM_In_0(I0),
    .Kbd_ASCII_Data(KDB_DATA), .RAM_In_1(I1), .TTY_Enable(TTY_EN), .RAM_In_2(I2), .RAM_In_3(I3), .Reset(RST),
    .RAM_Out_0(ram_1_data_out_0), .Clock(CLK), .RAM_Out_1(ram_1_data_out_1), .Kbd_Enable_2(halt),
    .RAM_Out_2(ram_1_data_out_2), .RAM_Out_3(ram_1_data_out_3), .Mask(Mask), .Read_Time(ram_1_read_time),
    .Write_Time(ram_1_write_time), .nRead_Write(R_W), .Chip_Select(CS), .TTY_DATA(TTY_DATA));
  D_Flip_Flop d_ff_3 (.clk(CLK), .D(d_ff_1_q), .Qn(LCLR), .reset(Reset_out));  // open: Q, preset, en
  or or_1 (RST, LCLR, LoadRAM);
  or or_2 (RST, LCLR, LoadRAM);
  Clock clock_1 (.out(CLK));
  Multiplexer #(.width(32), .enable("false")) multiplexer_1 (.in0(I0), .in1(LData), .out(RI0), .sel(LoadRAM));
  Multiplexer #(.width(32), .enable("false")) multiplexer_2 (.in0(I1), .in1(LData), .out(RI1), .sel(LoadRAM));
  Multiplexer #(.width(32), .enable("false")) multiplexer_3 (.in0(I2), .in1(LData), .out(RI2), .sel(LoadRAM));
  Multiplexer #(.width(32), .enable("false")) multiplexer_4 (.in0(I3), .in1(LData), .out(RI3), .sel(LoadRAM));
  and and_1 (LoadRAM, ~DESHABILITAR_DISPATCHER, LoadRAMOn);  // AND_Gate
  Multiplexer #(.width(16), .enable("false")) multiplexer_5 (.in0(Addr), .in1(LAddr), .out(RAddr), .sel(LoadRAM));
  Multiplexer #(.width(4), .enable("false")) multiplexer_6 (.in0(Mask), .in1(LMask), .out(RMask), .sel(LoadRAM));
  Multiplexer #(.enable("false")) multiplexer_7 (.in0(CS), .in1(LW), .out(RCS), .sel(LoadRAM));
  Multiplexer #(.enable("false")) multiplexer_8 (.in0(R_W), .in1(LW), .out(R_R_W), .sel(LoadRAM));

  // Notes on the sheet:
  //   NO MODIFICAR
  //   Keyboard
endmodule

module RAM (
  input  [15:0] Address,
  input  [31:0] Data_In_0,
  input  [31:0] Data_In_1,
  input  [31:0] Data_In_2,
  input  [31:0] Data_In_3,
  input  [3:0] Mask,
  input  nRead_Write,
  input  Chip_Select,
  input  Reset,
  output [31:0] Data_Out_0,
  output [31:0] Data_Out_1,
  output [31:0] Data_Out_2,
  output [31:0] Data_Out_3,
  output [3:0] Read_Time,
  output [3:0] Write_Time
);

  wire and_2_out, and_3_out, and_4_out, and_5_out, and_6_out, and_7_out, and_8_out, and_9_out, Changed, CLK,
       comparator_2_eq, comparator_3_eq, comparator_4_eq, comparator_5_eq, comparator_6_eq, Count,
       demultiplexer_3_out0, Idle, Idle_q, Load, Load0, Load1, nand_1_out, or_1_out, or_2_out, or_3_out,
       or_4_out, or_5_out, or_6_out, or_7_out, or_8_out, or_9_out, or_10_out, Proc_q, Update_Mem, Zero_Time;
  wire [3:0] counter_1_q, multiplexer_1_out, subtractor_1_out;
  wire [31:0] register_1_q, register_2_q, register_3_q, register_4_q, register_5_q;

  // Probe on 4'b0011
  // Probe on 4'b0010
  Multiplexer #(.width(4), .enable("false")) multiplexer_1 (
    .in0(4'b0011), .in1(4'b0010), .out(multiplexer_1_out), .sel(nRead_Write));
  or or_1 (or_1_out, Idle, Update_Mem);
  or or_2 (or_2_out, ~Chip_Select, Reset);  // OR_Gate
  Subtractor #(.width(4)) subtractor_1 (.a(multiplexer_1_out), .b(4'b0010), .out(subtractor_1_out));  // open: bin, bout
  Demultiplexer #(.enable("false")) demultiplexer_1 (.out0(Idle), .out1(Load0), .in(Idle_q), .sel(Changed));
  D_Flip_Flop u_Idle (.clk(CLK), .D(or_1_out), .Q(Idle_q), .preset(or_2_out));  // open: Qn, en, reset
  // Probe on counter_1_q
  Counter #(.width(4), .max('hf)) counter_1 (
    .load(Load), .D(subtractor_1_out), .count(Count), .Q(counter_1_q), .clk(CLK), .clr(or_3_out));  // open: carry
  or or_3 (or_3_out, ~Chip_Select, Reset);  // OR_Gate
  Comparator #(.width(4), .mode("unsigned")) comparator_1 (
    .a(4'b0000), .b(counter_1_q), .eq(Zero_Time));  // open: gt, lt
  or or_4 (or_4_out, Count, Load0, Load1);
  Register #(.width(32)) register_1 (.D(Data_In_0), .en(Chip_Select), .Q(register_1_q), .clk(CLK), .clr(or_5_out));
  or or_5 (or_5_out, ~Chip_Select, Reset);  // OR_Gate
  Register #(.width(32)) register_2 (.D(Data_In_1), .en(Chip_Select), .Q(register_2_q), .clk(CLK), .clr(or_6_out));
  or or_6 (or_6_out, ~Chip_Select, Reset);  // OR_Gate
  Register #(.width(32)) register_3 (.D(Data_In_2), .en(Chip_Select), .Q(register_3_q), .clk(CLK), .clr(or_7_out));
  or or_7 (or_7_out, ~Chip_Select, Reset);  // OR_Gate
  Register #(.width(32)) register_4 (.D(Data_In_3), .en(Chip_Select), .Q(register_4_q), .clk(CLK), .clr(or_8_out));
  or or_8 (or_8_out, ~Chip_Select, Reset);  // OR_Gate
  Register #(.width(32)) register_5 (
    .D({{11{1'b1}}, nRead_Write, Mask, Address}), .en(Chip_Select), .Q(register_5_q), .clk(CLK),
    .clr(or_9_out));
  or or_9 (or_9_out, ~Chip_Select, Reset);  // OR_Gate
  D_Flip_Flop Proc (.clk(CLK), .D(or_4_out), .Q(Proc_q), .reset(or_10_out));  // open: Qn, preset, en
  or or_10 (or_10_out, ~Chip_Select, Reset);  // OR_Gate
  Demultiplexer #(.enable("false")) demultiplexer_2 (
    .out0(Count), .out1(Update_Mem), .in(demultiplexer_3_out0), .sel(Zero_Time));
  Demultiplexer #(.enable("false")) demultiplexer_3 (
    .out0(demultiplexer_3_out0), .out1(Load1), .in(Proc_q), .sel(Changed));
  Demultiplexer #(.enable("false")) demultiplexer_4 (
    .out0(demultiplexer_3_out0), .out1(Load1), .in(Proc_q), .sel(Changed));
  Clock clock_1 (.out(CLK));
  Comparator #(.width(32)) comparator_2 (.a(register_1_q), .b(Data_In_0), .eq(comparator_2_eq));  // open: gt, lt
  Comparator #(.width(32)) comparator_3 (.a(register_2_q), .b(Data_In_1), .eq(comparator_3_eq));  // open: gt, lt
  Comparator #(.width(32)) comparator_4 (.a(register_3_q), .b(Data_In_2), .eq(comparator_4_eq));  // open: gt, lt
  Comparator #(.width(32)) comparator_5 (.a(register_4_q), .b(Data_In_3), .eq(comparator_5_eq));  // open: gt, lt
  Comparator #(.width(32)) comparator_6 (
    .a(register_5_q), .b({{11{1'b1}}, nRead_Write, Mask, Address}), .eq(comparator_6_eq));  // open: gt, lt
  nand nand_1 (nand_1_out, comparator_6_eq, comparator_2_eq, comparator_3_eq, comparator_4_eq, comparator_5_eq);
  and and_1 (Changed, nand_1_out, Chip_Select);
  or or_11 (Load, Count, Load1, Load0);
  and and_2 (and_2_out, Mask[0], Update_Mem, nRead_Write);
  and and_3 (and_3_out, Mask[1], Update_Mem, nRead_Write);
  and and_4 (and_4_out, Mask[2], Update_Mem, nRead_Write);
  and and_5 (and_5_out, Mask[3], Update_Mem, nRead_Write);
  RAM_part #(.addrWidth(16), .dataWidth(32), .bus("separate")) ram_1 (
    .addr(Address), .din(Data_In_0), .data(Data_Out_0), .str(and_2_out), .sel(Chip_Select), .clk(CLK),
    .ld(and_6_out), .clr(Reset));
  and and_6 (and_6_out, ~nRead_Write, Idle);  // AND_Gate
  RAM_part #(.addrWidth(16), .dataWidth(32), .bus("separate")) ram_2 (
    .addr(Address), .din(Data_In_1), .data(Data_Out_1), .str(and_3_out), .sel(Chip_Select), .clk(CLK),
    .ld(and_7_out), .clr(Reset));
  and and_7 (and_7_out, ~nRead_Write, Idle);  // AND_Gate
  RAM_part #(.addrWidth(16), .dataWidth(32), .bus("separate")) ram_3 (
    .addr(Address), .din(Data_In_2), .data(Data_Out_2), .str(and_4_out), .sel(Chip_Select), .clk(CLK),
    .ld(and_8_out), .clr(Reset));
  and and_8 (and_8_out, ~nRead_Write, Idle);  // AND_Gate
  RAM_part #(.addrWidth(16), .dataWidth(32), .bus("separate")) ram_4 (
    .addr(Address), .din(Data_In_3), .data(Data_Out_3), .str(and_5_out), .sel(Chip_Select), .clk(CLK),
    .ld(and_9_out), .clr(Reset));
  and and_9 (and_9_out, ~nRead_Write, Idle);  // AND_Gate

  assign Read_Time = 4'b0011;
  assign Write_Time = 4'b0010;

  // Other names for the same wires on the sheet: M0 = Mask[0]; M1 = Mask[1]; M2 = Mask[2]; M3 = Mask[3];
  //   RW = nRead_Write; CLR = Reset; CS = Chip_Select; Load2 = Count

  // Notes on the sheet:
  //   NO MODIFICAR
  //   excepto quizás los valores RT y WT
  //   BANK0
  //   BANK1
  //   BANK2
  //   BANK3
endmodule

module S_MIPS (
  input  Kbd_Available,
  input  [31:0] RAM_Out_0,
  input  [6:0] Kbd_ASCII_Data,
  input  [31:0] RAM_Out_1,
  input  [31:0] RAM_Out_2,
  input  Reset,
  input  Clock,
  input  [31:0] RAM_Out_3,
  input  [3:0] Read_Time,
  input  [3:0] Write_Time,
  output [15:0] Address,
  output Kbd_Enable,
  output Kbd_Clear,
  output TTY_Enable,
  output [6:0] TTY_DATA,
  output Kbd_Enable_2,
  output [31:0] RAM_In_0,
  output [31:0] RAM_In_1,
  output [31:0] RAM_In_2,
  output [31:0] RAM_In_3,
  output [3:0] Mask,
  output nRead_Write,
  output Chip_Select
);

  wire data_path_1_nf, data_path_1_zf, Load_Inst, Log_Imm_Op, PC, pop, push, R_W, rt_rd, Save_Data;
  wire [1:0] B_Select, Select_Address;
  wire [2:0] Branch_Op, DI_Select;
  wire [3:0] ALU_Op;
  wire [4:0] instruction_decoder_1_data_address, instruction_decoder_1_selector_a,
       instruction_decoder_1_selector_b;
  wire [5:0] instruction_decoder_1_function_code, instruction_decoder_1_operation_code;
  wire [15:0] offset;
  wire [25:0] address_t;
  wire [31:0] add_lw_sw, Address_In, Data_In, data_path_1_constant, From_PC, PC_prime, RAM_In, RT, Stack_P;
  wire [31:7] RS;

  RAM_Manager ram_manager_1 (
    .Address_In(Address_In), .Clk(Clock), .Rst(Reset), .Save_Data(Save_Data), .RAM_00(RAM_Out_0),
    .RAM_01(RAM_Out_1), .RAM_In(RAM_In), .RAM_02(RAM_Out_2), .RAM_03(RAM_Out_3), .Address_Out(Address),
    .RAM_00_2(RAM_In_0), .RAM_01_2(RAM_In_1), .RAM_Out(Data_In), .RAM_02_2(RAM_In_2), .RAM_03_2(RAM_In_3),
    .Mask(Mask));
  Multiplexer #(.select(2), .width(32), .enable("false")) multiplexer_1 (
    .in0(From_PC), .in1(add_lw_sw), .in2(Stack_P), .out(Address_In), .sel(Select_Address));  // open: in3
  // Probe on Data_In
  Multiplexer #(.width(32), .enable("false")) multiplexer_2 (.in0(RT), .in1({RS, TTY_DATA}), .out(RAM_In), .sel(push));
  Instruction_Decoder instruction_decoder_1 (
    .Load_Instruction(Load_Inst), .Clock(Clock), .Reset(Reset),
    .Data_Address(instruction_decoder_1_data_address), .Address(address_t),
    .Selector_A(instruction_decoder_1_selector_a), .Selector_B(instruction_decoder_1_selector_b),
    .Operation_Code(instruction_decoder_1_operation_code), .Offset(offset),
    .Function_Code(instruction_decoder_1_function_code), .Instruction(Data_In));
  Data_Path data_path_1 (
    .Data_In(Data_In), .Clock(Clock), .Reset(Reset), .PC_prime(PC_prime),
    .RS(instruction_decoder_1_selector_a), .RD(instruction_decoder_1_data_address), .Offset(offset),
    .RT(instruction_decoder_1_selector_b), .Log_Imm_Op(Log_Imm_Op), .ALU_Op(ALU_Op), .Write_PC(PC),
    .B_Selector(B_Select), .DI_Selector(DI_Select), .rt_rd(rt_rd), .R_W(R_W), .Push(push), .Pop(pop),
    .KBD_Available(Kbd_Available), .KBD_Data(Kbd_ASCII_Data), .RT_2(RT), .Add_lw_sw(add_lw_sw),
    .Stack_Pointer(Stack_P), .Constant(data_path_1_constant), .ZF(data_path_1_zf), .NF(data_path_1_nf),
    .PC(From_PC), .RS_2({RS, TTY_DATA}));
  Control_Unit control_unit_1 (
    .Op_C(instruction_decoder_1_operation_code), .Read_Time(Read_Time),
    .Func_C(instruction_decoder_1_function_code), .Write_Time(Write_Time), .Clk(Clock), .Rst(Reset),
    .ALU_Op(ALU_Op), .Branch_Op(Branch_Op), .Logical_Immediate_Op(Log_Imm_Op), .DI_Select(DI_Select),
    .pop(pop), .KBD_Enable(Kbd_Enable), .TTY_Enable(TTY_Enable), .Chip_Selector(Chip_Select),
    .RW_RAM(nRead_Write), .Load_PC(PC), .Load_Instruction(Load_Inst), .R_W(R_W), .rt_rd(rt_rd),
    .B_Selector(B_Select), .Select_Address(Select_Address), .Push(push), .Save_Data(Save_Data),
    .END(Kbd_Enable_2));
  // Probe on PC_prime
  Branch_Control branch_control_1 (
    .RS({RS, TTY_DATA}), .PC(From_PC), .Destiny(address_t), .Offset(data_path_1_constant),
    .Operation(Branch_Op), .ZF(data_path_1_zf), .NF(data_path_1_nf), .PC_prime(PC_prime));

  assign Kbd_Clear = Reset;

  // Other names for the same wires on the sheet: CLK = Clock; CS = Chip_Select; KBD_AVAIL = Kbd_Available;
  //   CLR = Reset; KBD_CLR = Reset; KBD_DATA[6:0] = Kbd_ASCII_Data; RAM_A[15:0] = Address;
  //   RAM_INPUT_0[31:0] = RAM_In_0; RAM_INPUT_1[31:0] = RAM_In_1; RAM_INPUT_2[31:0] = RAM_In_2;
  //   RAM_INPUT_3[31:0] = RAM_In_3; RAM_MASK[3:0] = Mask; RAM_OUTPUT_0[31:0] = RAM_Out_0;
  //   RAM_OUTPUT_1[31:0] = RAM_Out_1; RAM_OUTPUT_2[31:0] = RAM_Out_2; RAM_OUTPUT_3[31:0] = RAM_Out_3;
  //   RS[6:0] = TTY_DATA; RW = nRead_Write; STOP = Kbd_Enable_2

  // Notes on the sheet:
  //   RAM ADDRESS
  //   DATA FROM RAM
  //   DATA TO RAM
  //   DATA WRITE MASK
  //   RAM TIMING
  //   RAM CONTROL
  //   KEYBOARD
  //   TTY
  //   SEQUENCING
endmodule

module RAM_Dispatcher (
  input  [3:0] WriteTime,
  input  Clock,
  input  CLR,
  output [31:0] Data,
  output [15:0] Address,
  output [3:0] Mask,
  output Finished,
  output Write
);

  wire demultiplexer_2_out1, demultiplexer_3_out1, End, IDLE_q, IncAddr, Load, or_1_out, or_2_out, While_q,
       WriteEnd;
  wire [3:0] counter_1_q;
  wire [31:0] CurrentAddress_q;

  Counter #(.width(32), .max('hffffffff)) CurrentAddress (
    .count(IncAddr), .Q({CurrentAddress_q[31:18], Address, CurrentAddress_q[1:0]}), .clk(Clock), .clr(CLR));  // open: load, D, carry
  or or_1 (or_1_out, IncAddr, demultiplexer_3_out1, Finished);
  D_Flip_Flop IDLE (.clk(Clock), .D(or_1_out), .Q(IDLE_q), .preset(CLR));  // open: Qn, en, reset
  Demultiplexer #(.enable("false")) demultiplexer_1 (.out0(Load), .out1(Finished), .in(IDLE_q), .sel(End));
  D_Flip_Flop While (.clk(Clock), .D(or_2_out), .Q(While_q), .reset(CLR));  // open: Qn, preset, en
  or or_2 (or_2_out, Write, Load);
  RAM_part #(.addrWidth(18), .dataWidth(32)) ram_1 (
    .addr({Address, CurrentAddress_q[1:0]}), .data(Data), .clk(Clock));  // open: sel, ld, clr
  Demultiplexer #(.enable("false")) demultiplexer_2 (
    .out0(Write), .out1(demultiplexer_2_out1), .in(While_q), .sel(WriteEnd));
  Decoder #(.select(2)) decoder_1 (
    .out0(Mask[0]), .out1(Mask[1]), .out2(Mask[2]), .out3(Mask[3]), .sel(CurrentAddress_q[1:0]));  // open: en
  Demultiplexer #(.enable("false")) demultiplexer_3 (
    .out0(IncAddr), .out1(demultiplexer_3_out1), .in(demultiplexer_2_out1), .sel(End));
  Counter #(.width(4), .max('hf)) counter_1 (
    .load(Load), .D(WriteTime), .count(Write), .Q(counter_1_q), .clk(Clock));  // open: carry, clr
  Comparator #(.width(32)) comparator_1 (.a(Data), .b({32{1'b1}}), .eq(End));  // open: gt, lt
  Comparator #(.width(4)) comparator_2 (.a(4'b0000), .b(counter_1_q), .eq(WriteEnd));  // open: gt, lt

  // Other names for the same wires on the sheet: CLK = Clock; Count = Write; WT[3:0] = WriteTime
endmodule

module Register_File (
  input  [4:0] Data_Address,
  input  [31:0] Data_Input,
  input  Read_Write,
  input  Clock,
  input  Reset,
  input  Push,
  input  Pop,
  input  [4:0] Selector_A,
  input  [4:0] Selector_B,
  output [31:0] Data_A,
  output [31:0] Data_B,
  output [31:0] Stack_Pointer
);

  wire _0, _4, _8, _12, _16, _20, _24, _28, or_1_out;
  wire [1:0] priority_encoder_1_out;
  wire [3:1] _0_to_3, _4_to_7, _8_to_11, _12_to_15, _16_to_19, _20_to_23, _24_to_27, _28_to_31;
  wire [4:0] multiplexer_2_out;
  wire [31:0] adder_1_out, multiplexer_4_out, Q0, Q1, Q2, Q3, Q4, Q5, Q6, Q7, Q8, Q9, Q10, Q11, Q12, Q13,
       Q14, Q15, Q16, Q17, Q18, Q19, Q20, Q21, Q22, Q23, Q24, Q25, Q26, Q27, Q28, Q29, Q30, subtractor_1_out;

  Multiplexer #(.select(5), .width(32), .enable("false")) multiplexer_1 (
    .in0(Q0), .in1(Q1), .in2(Q2), .in3(Q3), .in4(Q4), .in5(Q5), .in6(Q6), .in7(Q7), .in8(Q8), .in9(Q9),
    .in10(Q10), .in11(Q11), .in12(Q12), .in13(Q13), .in14(Q14), .in15(Q15), .in16(Q16), .in17(Q17),
    .in18(Q18), .in19(Q19), .in20(Q20), .in21(Q21), .in22(Q22), .in23(Q23), .in24(Q24), .in25(Q25),
    .in26(Q26), .in27(Q27), .in28(Q28), .in29(Q29), .in30(Q30), .in31(Stack_Pointer), .out(Data_A),
    .sel(Selector_A));
  Decoder #(.select(5)) decoder_1 (
    .out0(_0), .out1(_0_to_3[1]), .out2(_0_to_3[2]), .out3(_0_to_3[3]), .out4(_4), .out5(_4_to_7[1]),
    .out6(_4_to_7[2]), .out7(_4_to_7[3]), .out8(_8), .out9(_8_to_11[1]), .out10(_8_to_11[2]),
    .out11(_8_to_11[3]), .out12(_12), .out13(_12_to_15[1]), .out14(_12_to_15[2]), .out15(_12_to_15[3]),
    .out16(_16), .out17(_16_to_19[1]), .out18(_16_to_19[2]), .out19(_16_to_19[3]), .out20(_20),
    .out21(_20_to_23[1]), .out22(_20_to_23[2]), .out23(_20_to_23[3]), .out24(_24), .out25(_24_to_27[1]),
    .out26(_24_to_27[2]), .out27(_24_to_27[3]), .out28(_28), .out29(_28_to_31[1]), .out30(_28_to_31[2]),
    .out31(_28_to_31[3]), .sel(multiplexer_2_out), .en(1'b1));
  Multiplexer #(.width(5), .enable("false")) multiplexer_2 (
    .in0({5{1'b0}}), .in1(Data_Address), .out(multiplexer_2_out), .sel(Read_Write));
  // Probe on Q1
  // Probe on Q2
  // Probe on Q3
  Multiplexer #(.select(5), .width(32), .enable("false")) multiplexer_3 (
    .in0(Q0), .in1(Q1), .in2(Q2), .in3(Q3), .in4(Q4), .in5(Q5), .in6(Q6), .in7(Q7), .in8(Q8), .in9(Q9),
    .in10(Q10), .in11(Q11), .in12(Q12), .in13(Q13), .in14(Q14), .in15(Q15), .in16(Q16), .in17(Q17),
    .in18(Q18), .in19(Q19), .in20(Q20), .in21(Q21), .in22(Q22), .in23(Q23), .in24(Q24), .in25(Q25),
    .in26(Q26), .in27(Q27), .in28(Q28), .in29(Q29), .in30(Q30), .in31(Stack_Pointer), .out(Data_B),
    .sel(Selector_B));
  Register #(.width(32)) Reg0 (.D({32{1'b0}}), .Q(Q0), .clk(Clock), .clr(Reset));  // open: en
  Register #(.width(32)) Reg1 (.D(Data_Input), .en(_0_to_3[1]), .Q(Q1), .clk(Clock), .clr(Reset));
  Register #(.width(32)) Reg7 (.D(Data_Input), .en(_4_to_7[3]), .Q(Q7), .clk(Clock), .clr(Reset));
  Register #(.width(32)) Reg13 (.D(Data_Input), .en(_12_to_15[1]), .Q(Q13), .clk(Clock), .clr(Reset));
  Register #(.width(32)) Reg19 (.D(Data_Input), .en(_16_to_19[3]), .Q(Q19), .clk(Clock), .clr(Reset));
  Register #(.width(32)) Reg25 (.D(Data_Input), .en(_24_to_27[1]), .Q(Q25), .clk(Clock), .clr(Reset));
  Register #(.width(32)) Reg2 (.D(Data_Input), .en(_0_to_3[2]), .Q(Q2), .clk(Clock), .clr(Reset));
  Register #(.width(32)) Reg8 (.D(Data_Input), .en(_8), .Q(Q8), .clk(Clock), .clr(Reset));
  Register #(.width(32)) Reg14 (.D(Data_Input), .en(_12_to_15[2]), .Q(Q14), .clk(Clock), .clr(Reset));
  Register #(.width(32)) Reg20 (.D(Data_Input), .en(_20), .Q(Q20), .clk(Clock), .clr(Reset));
  Register #(.width(32)) Reg26 (.D(Data_Input), .en(_24_to_27[2]), .Q(Q26), .clk(Clock), .clr(Reset));
  Register #(.width(32)) Reg3 (.D(Data_Input), .en(_0_to_3[3]), .Q(Q3), .clk(Clock), .clr(Reset));
  Register #(.width(32)) Reg9 (.D(Data_Input), .en(_8_to_11[1]), .Q(Q9), .clk(Clock), .clr(Reset));
  Register #(.width(32)) Reg15 (.D(Data_Input), .en(_12_to_15[3]), .Q(Q15), .clk(Clock), .clr(Reset));
  Register #(.width(32)) Reg21 (.D(Data_Input), .en(_20_to_23[1]), .Q(Q21), .clk(Clock), .clr(Reset));
  Register #(.width(32)) Reg27 (.D(Data_Input), .en(_24_to_27[3]), .Q(Q27), .clk(Clock), .clr(Reset));
  Register #(.width(32)) Reg4 (.D(Data_Input), .en(_4), .Q(Q4), .clk(Clock), .clr(Reset));
  Register #(.width(32)) Reg10 (.D(Data_Input), .en(_8_to_11[2]), .Q(Q10), .clk(Clock), .clr(Reset));
  Register #(.width(32)) Reg16 (.D(Data_Input), .en(_16), .Q(Q16), .clk(Clock), .clr(Reset));
  Register #(.width(32)) Reg22 (.D(Data_Input), .en(_20_to_23[2]), .Q(Q22), .clk(Clock), .clr(Reset));
  Register #(.width(32)) Reg28 (.D(Data_Input), .en(_28), .Q(Q28), .clk(Clock), .clr(Reset));
  Register #(.width(32)) Reg5 (.D(Data_Input), .en(_4_to_7[1]), .Q(Q5), .clk(Clock), .clr(Reset));
  Register #(.width(32)) Reg11 (.D(Data_Input), .en(_8_to_11[3]), .Q(Q11), .clk(Clock), .clr(Reset));
  Register #(.width(32)) Reg17 (.D(Data_Input), .en(_16_to_19[1]), .Q(Q17), .clk(Clock), .clr(Reset));
  Register #(.width(32)) Reg23 (.D(Data_Input), .en(_20_to_23[3]), .Q(Q23), .clk(Clock), .clr(Reset));
  Register #(.width(32)) Reg29 (.D(Data_Input), .en(_28_to_31[1]), .Q(Q29), .clk(Clock), .clr(Reset));
  Register #(.width(32)) Reg6 (.D(Data_Input), .en(_4_to_7[2]), .Q(Q6), .clk(Clock), .clr(Reset));
  Register #(.width(32)) Reg11_2 (.D(Data_Input), .en(_12), .Q(Q12), .clk(Clock), .clr(Reset));
  Register #(.width(32)) Reg18 (.D(Data_Input), .en(_16_to_19[2]), .Q(Q18), .clk(Clock), .clr(Reset));
  Register #(.width(32)) Reg24 (.D(Data_Input), .en(_24), .Q(Q24), .clk(Clock), .clr(Reset));
  Register #(.width(32)) Reg30 (.D(Data_Input), .en(_28_to_31[2]), .Q(Q30), .clk(Clock), .clr(Reset));
  Adder #(.width(32)) adder_1 (.a(Stack_Pointer), .b(32'h4), .out(adder_1_out));  // open: cin, cout
  Subtractor #(.width(32)) subtractor_1 (.a(Stack_Pointer), .b(32'h4), .out(subtractor_1_out));  // open: bin, bout
  Priority_Encoder #(.select(2)) priority_encoder_1 (
    .in0(1'b1), .in1(Pop), .in2(Push), .in3(Reset), .out(priority_encoder_1_out));
  Multiplexer #(.select(2), .width(32), .enable("false")) multiplexer_4 (
    .in0(Data_Input), .in1(adder_1_out), .in2(subtractor_1_out), .in3(32'h3ffff), .out(multiplexer_4_out),
    .sel(priority_encoder_1_out));
  or or_1 (or_1_out, _28_to_31[3], Pop, Push, Reset);
  Register #(.width(32)) R31_Stack__Pointer (
    .D(multiplexer_4_out), .en(or_1_out), .Q(Stack_Pointer), .clk(Clock));  // open: clr

  // Other names for the same wires on the sheet: _0_to_3[0] = _0; _1 = _0_to_3[1]; _2 = _0_to_3[2]; _3 = _0_to_3[3];
  //   _4_to_7[0] = _4; _5 = _4_to_7[1]; _6 = _4_to_7[2]; _7 = _4_to_7[3]; _8_to_11[0] = _8; _9 = _8_to_11[1];
  //   _10 = _8_to_11[2]; _11 = _8_to_11[3]; _12_to_15[0] = _12; _13 = _12_to_15[1]; _14 = _12_to_15[2];
  //   _15 = _12_to_15[3]; _16_to_19[0] = _16; _17 = _16_to_19[1]; _18 = _16_to_19[2]; _19 = _16_to_19[3];
  //   _20_to_23[0] = _20; _21 = _20_to_23[1]; _22 = _20_to_23[2]; _23 = _20_to_23[3]; _24_to_27[0] = _24;
  //   _25 = _24_to_27[1]; _26 = _24_to_27[2]; _27 = _24_to_27[3]; _28_to_31[0] = _28; _29 = _28_to_31[1];
  //   _30 = _28_to_31[2]; _31 = _28_to_31[3]; A[4:0] = Selector_A; B[4:0] = Selector_B; clk = Clock;
  //   Q31[31:0] = Stack_Pointer; R_W = Read_Write; res = Reset

  // Notes on the sheet:
  //   INPUT ZONE
  //   Reading Controler
  //   Writing Controler
  //   REGISTER ZONE
  //   OUTPUT ZONE
endmodule

module ALU (
  input  [31:0] A,
  input  [31:0] B,
  input  [3:0] ALU_op,
  output [31:0] Output,
  output Zero,
  output Zero_2,
  output [31:0] Hi,
  output [31:0] Lo
);

  wire comparator_1_lt, comparator_2_lt;
  wire [31:0] AND, div_hi, div_lo, divu_hi, divu_lo, mul_hi, mul_lo, mulu_hi, mulu_lo, NOR, OR, tunnel,
       tunnel_t, tunnel_t_t, u, XOR;

  // Probe on A
  // Probe on B
  Adder #(.width(32)) adder_1 (.a(A), .b(B), .out(tunnel));  // open: cin, cout
  Subtractor #(.width(32)) subtractor_1 (.a(A), .b(B), .out(tunnel_t));  // open: bin, bout
  Comparator #(.width(32), .mode("unsigned")) comparator_1 (.a(A), .b(B), .lt(comparator_1_lt));  // open: gt, eq
  Comparator #(.width(32)) comparator_2 (.a(A), .b(B), .lt(comparator_2_lt));  // open: gt, eq
  Multiplier #(.width(32)) multiplier_1 (.a(A), .b(B), .out(mulu_lo), .cout(mulu_hi));  // open: cin
  Mult_i mult_i_1 (.A(A), .B(B), .Hi(mul_hi), .Lo(mul_lo));
  Multiplexer #(.width(32), .enable("false")) multiplexer_1 (
    .in0({32{1'b0}}), .in1(32'h1), .out(u), .sel(comparator_1_lt));
  Multiplexer #(.width(32), .enable("false")) multiplexer_2 (
    .in0({32{1'b0}}), .in1(32'h1), .out(tunnel_t_t), .sel(comparator_2_lt));
  assign AND = A & B;  // AND_Gate and_1, 32 bits wide
  assign OR = A | B;  // OR_Gate or_1, 32 bits wide
  Divider #(.width(32)) divider_1 (.a(A), .b(B), .out(divu_lo), .rem(divu_hi));  // open: upper
  assign XOR = A ^ B;  // XOR_Gate xor_1, 32 bits wide
  assign NOR = ~(A | B);  // NOR_Gate nor_1, 32 bits wide
  Div_i div_i_1 (.A(A), .B(B), .Hi(div_hi), .Lo(div_lo));
  // Probe on ALU_op[2:0]
  // Probe on Output
  Multiplexer #(.select(3), .width(32), .enable("false")) multiplexer_3 (
    .in0(tunnel), .in1(tunnel_t), .in2(AND), .in3(OR), .in4(NOR), .in5(XOR), .in6(tunnel_t_t), .in7(u),
    .out(Output), .sel(ALU_op[2:0]));
  Multiplexer #(.select(2), .width(32), .enable("false")) multiplexer_4 (
    .in0(mul_hi), .in1(mulu_hi), .in2(div_hi), .in3(divu_hi), .out(Hi), .sel(ALU_op[1:0]));
  Multiplexer #(.select(2), .width(32), .enable("false")) multiplexer_5 (
    .in0(mul_lo), .in1(mulu_lo), .in2(div_lo), .in3(divu_lo), .out(Lo), .sel(ALU_op[1:0]));
  // Probe on Hi
  // Probe on Lo
  Comparator #(.width(32), .mode("unsigned")) comparator_3 (.a({32{1'b0}}), .b(Output), .eq(Zero_2));  // open: gt, lt

  assign Zero = Output[31];

  // Other names for the same wires on the sheet: Select[2:0] = ALU_op[2:0]; Select_Hi_Lo[1:0] = ALU_op[1:0]

  // Notes on the sheet:
  //   Inputs
  //   Basic Ops
  //   Multiplication and Division
  //   Outputs
  //   Outputs Hi/Lo
endmodule

module Mult_i (
  input  [31:0] A,
  input  [31:0] B,
  output [31:0] Hi,
  output [31:0] Lo
);

  wire adder_1_cout, adder_3_cout;
  wire [31:0] _00_hi, _00_lo, _01_hi, _01_lo, _10_hi, _10_lo, _11_hi, _11_lo, bit_extender_1_out,
       bit_extender_2_out, multiplier_3_cout, multiplier_3_out, multiplier_4_cout, multiplier_4_out,
       nand_1_out, nand_2_out, nand_3_out, nand_4_out, negator_1_out, negator_2_out, negator_3_out,
       negator_4_out;

  Multiplexer #(.select(2), .width(32), .enable("false")) multiplexer_1 (
    .in0(_00_hi), .in1(_01_hi), .in2(_10_hi), .in3(_11_hi), .out(Hi), .sel({A[31], B[31]}));
  Multiplexer #(.select(2), .width(32), .enable("false")) multiplexer_2 (
    .in0(_00_lo), .in1(_01_lo), .in2(_10_lo), .in3(_11_lo), .out(Lo), .sel({A[31], B[31]}));
  // Probe on A
  // Probe on B
  // Probe on Hi
  // Probe on Lo
  Negator #(.width(32)) negator_1 (.in(A), .out(negator_1_out));
  Negator #(.width(32)) negator_2 (.in(B), .out(negator_2_out));
  Multiplier #(.width(32)) multiplier_1 (.a(A), .b(B), .out(_00_lo), .cout(_00_hi));  // open: cin
  Multiplier #(.width(32)) multiplier_2 (
    .a(negator_1_out), .b(negator_2_out), .out(_11_lo), .cout(_11_hi));  // open: cin
  Negator #(.width(32)) negator_3 (.in(B), .out(negator_3_out));
  Negator #(.width(32)) negator_4 (.in(A), .out(negator_4_out));
  Multiplier #(.width(32)) multiplier_3 (
    .a(A), .b(negator_3_out), .out(multiplier_3_out), .cout(multiplier_3_cout));  // open: cin
  Multiplier #(.width(32)) multiplier_4 (
    .a(negator_4_out), .b(B), .out(multiplier_4_out), .cout(multiplier_4_cout));  // open: cin
  assign nand_1_out = ~(multiplier_3_out & {32{1'b1}});  // NAND_Gate nand_1, 32 bits wide
  assign nand_2_out = ~({32{1'b1}} & multiplier_3_cout);  // NAND_Gate nand_2, 32 bits wide
  assign bit_extender_1_out = {{31{1'b0}}, adder_1_cout};  // Bit_Extender bit_extender_1
  assign nand_3_out = ~(multiplier_4_out & {32{1'b1}});  // NAND_Gate nand_3, 32 bits wide
  assign nand_4_out = ~({32{1'b1}} & multiplier_4_cout);  // NAND_Gate nand_4, 32 bits wide
  assign bit_extender_2_out = {{31{1'b0}}, adder_3_cout};  // Bit_Extender bit_extender_2
  Adder #(.width(32)) adder_1 (.a(nand_1_out), .b(32'h1), .out(_01_lo), .cout(adder_1_cout));  // open: cin
  Adder #(.width(32)) adder_2 (.a(nand_2_out), .b(bit_extender_1_out), .out(_01_hi));  // open: cin, cout
  Adder #(.width(32)) adder_3 (.a(nand_3_out), .b(32'h1), .out(_10_lo), .cout(adder_3_cout));  // open: cin
  Adder #(.width(32)) adder_4 (.a(nand_4_out), .b(bit_extender_2_out), .out(_10_hi));  // open: cin, cout

  // Other names for the same wires on the sheet: Sign_B = B[31]; Sign_A = A[31]

  // Notes on the sheet:
  //   Inputs
  //   Outputs
  //   Positive Positive
  //   Negative Negative
  //   Positive Negative
  //    Negative Positive
endmodule

module Div_i (
  input  [31:0] A,
  input  [31:0] B,
  output [31:0] Hi,
  output [31:0] Lo
);

  wire [31:0] _00_hi, _00_lo, _01_hi, _01_lo, _10_hi, _10_lo, _11_hi, _11_lo, divider_3_out, divider_4_out,
       negator_1_out, negator_2_out, negator_3_out, negator_4_out;

  Multiplexer #(.select(2), .width(32), .enable("false")) multiplexer_1 (
    .in0(_00_hi), .in1(_01_hi), .in2(_10_hi), .in3(_11_hi), .out(Hi), .sel({A[31], B[31]}));
  Multiplexer #(.select(2), .width(32), .enable("false")) multiplexer_2 (
    .in0(_00_lo), .in1(_01_lo), .in2(_10_lo), .in3(_11_lo), .out(Lo), .sel({A[31], B[31]}));
  // Probe on Hi
  // Probe on Lo
  // Probe on A
  // Probe on B
  Divider #(.width(32)) divider_1 (.a(A), .b(B), .out(_00_lo), .rem(_00_hi));  // open: upper
  Negator #(.width(32)) negator_1 (.in(A), .out(negator_1_out));
  Negator #(.width(32)) negator_2 (.in(B), .out(negator_2_out));
  Divider #(.width(32)) divider_2 (.a(negator_1_out), .b(negator_2_out), .out(_11_lo), .rem(_11_hi));  // open: upper
  Negator #(.width(32)) negator_3 (.in(B), .out(negator_3_out));
  Negator #(.width(32)) negator_4 (.in(A), .out(negator_4_out));
  Divider #(.width(32)) divider_3 (.a(A), .b(negator_3_out), .out(divider_3_out), .rem(_01_hi));  // open: upper
  Divider #(.width(32)) divider_4 (.a(negator_4_out), .b(B), .out(divider_4_out), .rem(_10_hi));  // open: upper
  Negator #(.width(32)) negator_5 (.in(divider_3_out), .out(_01_lo));
  Negator #(.width(32)) negator_6 (.in(divider_4_out), .out(_10_lo));

  // Other names for the same wires on the sheet: A_t[31:0] = A; Sign_A = A[31]; B_t[31:0] = B; Sign_B = B[31]

  // Notes on the sheet:
  //   Inputs
  //   Outputs
  //   Positive Positive
  //   Negative Negative
  //   Positive Negative
  //   Negative Positive
endmodule

module Branch_Control (
  input  [31:0] RS,
  input  [31:0] PC,
  input  [25:0] Destiny,
  input  [31:0] Offset,
  input  [2:0] Operation,
  input  ZF,
  input  NF,
  output [31:0] PC_prime
);

  wire and_1_out, and_2_out, and_3_out, and_4_out, and_5_out, beq, bgtz, blez, bltz, bne, branch, j, jr, nop,
       RS__0;
  wire [1:0] Select;
  wire [31:0] Branch_Amount, multiplier_1_out, Regular;
  wire [31:28] J_Jump;

  or or_1 (RS__0, ZF, NF);
  Decoder #(.select(3), .enable("false")) decoder_1 (
    .out0(nop), .out1(beq), .out2(bne), .out3(blez), .out4(bgtz), .out5(bltz), .out6(j), .out7(jr),
    .sel(Operation));
  Adder #(.width(32)) adder_1 (.a(PC), .b(32'h4), .out(Regular));  // open: cin, cout
  Multiplier #(.width(32)) multiplier_1 (.a(32'h4), .b(Offset), .out(multiplier_1_out));  // open: cin, cout
  Priority_Encoder #(.select(2)) priority_encoder_1 (
    .in0(1'b1), .in1(branch), .in2(j), .in3(jr), .out(Select), .en_in(1'b1));  // open: gs, en_out
  Adder #(.width(32)) adder_2 (.a(Regular), .b(multiplier_1_out), .out(Branch_Amount));  // open: cin, cout
  and and_1 (and_1_out, beq, ZF);
  and and_2 (and_2_out, bne, ~ZF);  // AND_Gate
  and and_3 (and_3_out, blez, RS__0);
  and and_4 (and_4_out, bgtz, ~RS__0);  // AND_Gate
  and and_5 (and_5_out, bltz, NF);
  BitSelector #(.width(32), .group(4)) bitselector_1 (.in(PC), .out(J_Jump), .sel(3'b111));
  or or_2 (branch, and_1_out, and_2_out, and_3_out, and_4_out, and_5_out);
  Multiplexer #(.select(2), .width(32), .enable("false")) multiplexer_1 (
    .in0(Regular), .in1(Branch_Amount), .in2({J_Jump, Destiny, 2'b00}), .in3(RS), .out(PC_prime), .sel(Select));

  // Other names for the same wires on the sheet: J_Jump[27:2] = Destiny; Op[2:0] = Operation

  // Notes on the sheet:
  //   Inputs
  //   Operations
  //   Selection Process
  //   PC Transformation
  //   I-Instructions
  //   Outputs
endmodule

module Instruction_Decoder (
  input  [31:0] Instruction,
  input  Load_Instruction,
  input  Clock,
  input  Reset,
  output [4:0] Data_Address,
  output [25:0] Address,
  output [4:0] Selector_A,
  output [4:0] Selector_B,
  output [5:0] Operation_Code,
  output [15:0] Offset,
  output [5:0] Function_Code
);

  Register #(.width(32)) Current_Instruction (
    .D(Instruction), .en(Load_Instruction), .Q({Operation_Code, Address}), .clk(Clock), .clr(Reset));

  assign Data_Address = Address[15:11];
  assign Function_Code = Address[5:0];
  assign Offset = Address[15:0];
  assign Selector_A = Address[25:21];
  assign Selector_B = Address[20:16];

  // Other names for the same wires on the sheet: Immediate[15:0] = Address[15:0]; Rd[4:0] = Address[15:11];
  //   Rt[4:0] = Address[20:16]; Rs[4:0] = Address[25:21]; clk = Clock; Instuc[31:0] = Instruction;
  //   Load_Instuc = Load_Instruction; res = Reset

  // Notes on the sheet:
  //   INPUT ZONE
  //   OUTPUT ZONE
endmodule

module Data_Path (
  input  [31:0] Data_In,
  input  Clock,
  input  Reset,
  input  [31:0] PC_prime,
  input  [4:0] RS,
  input  [4:0] RD,
  input  [15:0] Offset,
  input  [4:0] RT,
  input  Log_Imm_Op,
  input  [3:0] ALU_Op,
  input  Write_PC,
  input  [1:0] B_Selector,
  input  [2:0] DI_Selector,
  input  rt_rd,
  input  R_W,
  input  Push,
  input  Pop,
  input  KBD_Available,
  input  [6:0] KBD_Data,
  output [31:0] RT_2,
  output [31:0] Add_lw_sw,
  output [31:0] Stack_Pointer,
  output [31:0] PC,
  output [31:0] RS_2,
  output [31:0] Constant,
  output ZF,
  output NF
);

  wire and_1_out;
  wire [4:0] multiplexer_1_out;
  wire [6:0] KBD_D;
  wire [31:0] alu_1_hi, alu_1_lo, bit_extender_1_out, Hi, Lo, multiplexer_2_out, multiplexer_4_out,
       Random_out, RF_input, tunnel;

  assign bit_extender_1_out = {{25{KBD_D[6]}}, KBD_D};  // Bit_Extender bit_extender_1
  Multiplexer #(.width(5), .enable("false")) multiplexer_1 (.in0(RT), .in1(RD), .out(multiplexer_1_out), .sel(rt_rd));
  Register #(.width(32)) Program_Counter (.D(PC_prime), .en(Write_PC), .Q(PC), .clk(Clock), .clr(Reset));
  Multiplexer #(.width(32), .enable("false")) multiplexer_2 (
    .in0({32{1'b1}}), .in1(bit_extender_1_out), .out(multiplexer_2_out), .sel(KBD_Available));
  Random #(.width(32), .seed(212)) Random (.clk(Clock), .next(1'b1), .out(Random_out), .clr(Reset));
  Multiplexer #(.select(3), .width(32), .enable("false")) multiplexer_3 (
    .in0(Add_lw_sw), .in1(Data_In), .in2(Hi), .in3(Lo), .in4(multiplexer_2_out), .in5(Random_out),
    .out(RF_input), .sel(DI_Selector));  // open: in6, in7
  Register_File register_file_1 (
    .Clock(Clock), .Reset(Reset), .Push(Push), .Pop(Pop), .Read_Write(R_W), .Data_Input(RF_input),
    .Data_Address(multiplexer_1_out), .Selector_A(RS), .Selector_B(RT), .Data_A(RS_2), .Data_B(RT_2),
    .Stack_Pointer(Stack_Pointer));
  Sign_Extender sign_extender_1 (.Data_In(Offset), .Operation(Log_Imm_Op), .Data_Out(Constant));
  // Probe on RS_2
  // Probe on multiplexer_4_out
  Multiplexer #(.select(2), .width(32), .enable("false")) multiplexer_4 (
    .in0(RT_2), .in1({32{1'b0}}), .in2(Constant), .in3(tunnel), .out(multiplexer_4_out), .sel(B_Selector));
  // Probe on ALU_Op
  ALU alu_1 (
    .B(multiplexer_4_out), .ALU_op(ALU_Op), .Output(Add_lw_sw), .Zero(NF), .Zero_2(ZF), .Hi(alu_1_hi),
    .Lo(alu_1_lo), .A(RS_2));
  and and_1 (and_1_out, ALU_Op[3], ~ALU_Op[2]);  // AND_Gate
  Register #(.width(32)) u_Hi (.D(alu_1_hi), .en(and_1_out), .Q(Hi), .clk(Clock), .clr(Reset));
  Register #(.width(32)) u_Lo (.D(alu_1_lo), .en(and_1_out), .Q(Lo), .clk(Clock), .clr(Reset));

  // Other names for the same wires on the sheet: ALU_out[31:0] = Add_lw_sw; clk = Clock; KBD_A = KBD_Available;
  //   RS_t[31:0] = RS_2; rst = Reset; RT_t[31:0] = RT_2; SP[31:0] = Stack_Pointer

  // Notes on the sheet:
  //   Inputs
  //   RAM
  //   Branch Control
  //   Instruction Decoder
  //   Control Unit
  //   Keyboard
  //   Register File Input Selector
  //   To Branch Control
  //   Outputs
  //   To RAM
endmodule

module Sign_Extender (
  input  [15:0] Data_In,
  input  Operation,
  output [31:0] Data_Out
);

  wire [31:0] bit_extender_1_out, bit_extender_2_out;

  assign bit_extender_1_out = {{16{Data_In[15]}}, Data_In};  // Bit_Extender bit_extender_1
  assign bit_extender_2_out = {{16{1'b0}}, Data_In};  // Bit_Extender bit_extender_2
  Multiplexer #(.width(32), .enable("false")) multiplexer_1 (
    .in0(bit_extender_1_out), .in1(bit_extender_2_out), .out(Data_Out), .sel(Operation));

  // Other names for the same wires on the sheet: Op = Operation

  // Notes on the sheet:
  //   Inputs
  //   Outputs
endmodule

module Operation_Decoder (
  input  [5:0] OP_Code,
  input  [5:0] FUNC_Code,
  output [2:0] CU_Op,
  output [2:0] BC_Op,
  output [3:0] ALU_Op,
  output [1:0] B_Select,
  output [2:0] DI_Select,
  output [1:0] Special_Op,
  output Log_Imm_Op,
  output rt_rd,
  output lw,
  output pop
);

  wire add, addi, adds, ALU_OP_t, \and , and_11_out, and_13_out, and_15_out, and_17_out, and_19_out,
       and_21_out, and_29_out, and_31_out, and_32_out, and_33_out, and_34_out, and_35_out, and_36_out,
       and_45_out, and_46_out, and_47_out, and_51_out, and_52_out, and_55_out, and_56_out, and_57_out,
       and_58_out, and_63_out, andi, ands, B_Jump, beq, bgtz, blez, bltz, bne, Branch_OP, div, divu,
       F_000000, halt, Immediate_OP, j, jr, kbd, mfhi, mflo, mult, Mult_Div_OP, mulu, nop, \nor , OP_000000,
       OP_111000, OP_111111, \or , or_17_out, or_19_out, or_20_out, or_21_out, ori, ors, push, RAM_OP,
       Register_OP, rnd, sliti, slitiu, slt, slts, sltu, sltus, Special_OP_t, Stack_OP, sub, subs, sw, tty,
       \xor , xori, xors;

  // Probe on OP_Code
  // Probe on FUNC_Code
  and and_1 (OP_000000, ~OP_Code[0], ~OP_Code[1], ~OP_Code[2], ~OP_Code[3], ~OP_Code[4], ~OP_Code[5]);  // AND_Gate
  and and_2 (OP_111000, ~OP_Code[0], ~OP_Code[1], ~OP_Code[2], OP_Code[3], OP_Code[4], OP_Code[5]);  // AND_Gate
  and and_3 (OP_111111, OP_Code[0], OP_Code[1], OP_Code[2], OP_Code[3], OP_Code[4], OP_Code[5]);
  and and_4 (F_000000, ~FUNC_Code[0], ~FUNC_Code[1], ~FUNC_Code[2], ~FUNC_Code[3], ~FUNC_Code[4], ~FUNC_Code[5]);  // AND_Gate
  and and_5 (addi, ~OP_Code[0], ~OP_Code[1], ~OP_Code[2], OP_Code[3], ~OP_Code[4], ~OP_Code[5]);  // AND_Gate
  and and_6 (sliti, ~OP_Code[0], OP_Code[1], ~OP_Code[2], OP_Code[3], ~OP_Code[4], ~OP_Code[5]);  // AND_Gate
  and and_7 (slitiu, OP_Code[0], OP_Code[1], ~OP_Code[2], OP_Code[3], ~OP_Code[4], ~OP_Code[5]);  // AND_Gate
  and and_8 (andi, ~OP_Code[0], ~OP_Code[1], OP_Code[2], OP_Code[3], ~OP_Code[4], ~OP_Code[5]);  // AND_Gate
  and and_9 (ori, OP_Code[0], ~OP_Code[1], OP_Code[2], OP_Code[3], ~OP_Code[4], ~OP_Code[5]);  // AND_Gate
  and and_10 (xori, ~OP_Code[0], OP_Code[1], OP_Code[2], OP_Code[3], ~OP_Code[4], ~OP_Code[5]);  // AND_Gate
  and and_11 (and_11_out, ~FUNC_Code[0], ~FUNC_Code[1], ~FUNC_Code[2], ~FUNC_Code[3], ~FUNC_Code[4], FUNC_Code[5]);  // AND_Gate
  and and_12 (add, and_11_out, OP_000000);
  and and_13 (and_13_out, ~FUNC_Code[0], FUNC_Code[1], ~FUNC_Code[2], ~FUNC_Code[3], ~FUNC_Code[4], FUNC_Code[5]);  // AND_Gate
  and and_14 (sub, and_13_out, OP_000000);
  and and_15 (and_15_out, ~FUNC_Code[0], ~FUNC_Code[1], ~FUNC_Code[2], FUNC_Code[3], FUNC_Code[4], ~FUNC_Code[5]);  // AND_Gate
  and and_16 (mult, and_15_out, OP_000000);
  and and_17 (and_17_out, FUNC_Code[0], ~FUNC_Code[1], ~FUNC_Code[2], FUNC_Code[3], FUNC_Code[4], ~FUNC_Code[5]);  // AND_Gate
  and and_18 (mulu, and_17_out, OP_000000);
  and and_19 (and_19_out, ~FUNC_Code[0], FUNC_Code[1], ~FUNC_Code[2], FUNC_Code[3], FUNC_Code[4], ~FUNC_Code[5]);  // AND_Gate
  and and_20 (div, and_19_out, OP_000000);
  and and_21 (and_21_out, FUNC_Code[0], FUNC_Code[1], ~FUNC_Code[2], FUNC_Code[3], FUNC_Code[4], ~FUNC_Code[5]);  // AND_Gate
  and and_22 (divu, and_21_out, OP_000000);
  and and_23 (beq, ~OP_Code[0], ~OP_Code[1], OP_Code[2], ~OP_Code[3], ~OP_Code[4], ~OP_Code[5]);  // AND_Gate
  and and_24 (bne, OP_Code[0], ~OP_Code[1], OP_Code[2], ~OP_Code[3], ~OP_Code[4], ~OP_Code[5]);  // AND_Gate
  and and_25 (blez, ~OP_Code[0], OP_Code[1], OP_Code[2], ~OP_Code[3], ~OP_Code[4], ~OP_Code[5]);  // AND_Gate
  and and_26 (bgtz, OP_Code[0], OP_Code[1], OP_Code[2], ~OP_Code[3], ~OP_Code[4], ~OP_Code[5]);  // AND_Gate
  and and_27 (bltz, OP_Code[0], ~OP_Code[1], ~OP_Code[2], ~OP_Code[3], ~OP_Code[4], ~OP_Code[5]);  // AND_Gate
  and and_28 (j, ~OP_Code[0], OP_Code[1], ~OP_Code[2], ~OP_Code[3], ~OP_Code[4], ~OP_Code[5]);  // AND_Gate
  and and_29 (and_29_out, ~OP_Code[0], ~OP_Code[1], ~OP_Code[2], ~OP_Code[3], ~OP_Code[4], ~OP_Code[5]);  // AND_Gate
  and and_30 (nop, and_29_out, F_000000);
  and and_31 (and_31_out, ~FUNC_Code[0], ~FUNC_Code[1], FUNC_Code[2], ~FUNC_Code[3], ~FUNC_Code[4], FUNC_Code[5]);  // AND_Gate
  and and_32 (and_32_out, FUNC_Code[0], ~FUNC_Code[1], FUNC_Code[2], ~FUNC_Code[3], ~FUNC_Code[4], FUNC_Code[5]);  // AND_Gate
  and and_33 (and_33_out, FUNC_Code[0], FUNC_Code[1], FUNC_Code[2], ~FUNC_Code[3], ~FUNC_Code[4], FUNC_Code[5]);  // AND_Gate
  and and_34 (and_34_out, ~FUNC_Code[0], ~FUNC_Code[1], ~FUNC_Code[2], FUNC_Code[3], ~FUNC_Code[4], FUNC_Code[5]);  // AND_Gate
  and and_35 (and_35_out, ~FUNC_Code[0], FUNC_Code[1], ~FUNC_Code[2], FUNC_Code[3], ~FUNC_Code[4], FUNC_Code[5]);  // AND_Gate
  and and_36 (and_36_out, FUNC_Code[0], FUNC_Code[1], ~FUNC_Code[2], FUNC_Code[3], ~FUNC_Code[4], FUNC_Code[5]);  // AND_Gate
  and and_37 (\and , and_31_out, OP_000000);
  and and_38 (\or , and_32_out, OP_000000);
  and and_39 (\nor , and_33_out, OP_000000);
  and and_40 (\xor , and_34_out, OP_000000);
  and and_41 (slt, and_35_out, OP_000000);
  and and_42 (sltu, and_36_out, OP_000000);
  and and_43 (lw, OP_Code[0], OP_Code[1], ~OP_Code[2], ~OP_Code[3], ~OP_Code[4], OP_Code[5]);  // AND_Gate
  and and_44 (sw, OP_Code[0], OP_Code[1], ~OP_Code[2], OP_Code[3], ~OP_Code[4], OP_Code[5]);  // AND_Gate
  and and_45 (and_45_out, ~FUNC_Code[0], ~FUNC_Code[1], ~FUNC_Code[2], FUNC_Code[3], ~FUNC_Code[4], ~FUNC_Code[5]);  // AND_Gate
  and and_46 (and_46_out, ~FUNC_Code[0], ~FUNC_Code[1], ~FUNC_Code[2], ~FUNC_Code[3], FUNC_Code[4], ~FUNC_Code[5]);  // AND_Gate
  and and_47 (and_47_out, ~FUNC_Code[0], FUNC_Code[1], ~FUNC_Code[2], ~FUNC_Code[3], FUNC_Code[4], ~FUNC_Code[5]);  // AND_Gate
  or or_1 (ALU_OP_t, add, sub, mult, mulu, div, divu, slt, sltu, \and , \or , \nor , \xor );
  or or_2 (Branch_OP, nop, beq, bne, blez, bgtz, bltz, j, jr);
  or or_3 (Immediate_OP, addi, sliti, slitiu, andi, ori, xori);
  or or_4 (Log_Imm_Op, andi, ori, xori);
  and and_48 (jr, and_45_out, OP_000000);
  and and_49 (mfhi, and_46_out, OP_000000);
  and and_50 (mflo, and_47_out, OP_000000);
  or or_5 (Special_OP_t, halt, rnd, kbd, tty);
  or or_6 (Stack_OP, pop, push);
  or or_7 (RAM_OP, lw, sw);
  or or_8 (Register_OP, mfhi, mflo);
  or or_9 (Mult_Div_OP, mult, mulu, div, divu);
  and and_51 (and_51_out, ~FUNC_Code[0], ~FUNC_Code[1], ~FUNC_Code[2], ~FUNC_Code[3], ~FUNC_Code[4], ~FUNC_Code[5]);  // AND_Gate
  and and_52 (and_52_out, FUNC_Code[0], ~FUNC_Code[1], ~FUNC_Code[2], ~FUNC_Code[3], ~FUNC_Code[4], ~FUNC_Code[5]);  // AND_Gate
  and and_53 (pop, and_51_out, OP_111000);
  and and_54 (push, and_52_out, OP_111000);
  and and_55 (and_55_out, FUNC_Code[0], FUNC_Code[1], FUNC_Code[2], FUNC_Code[3], FUNC_Code[4], FUNC_Code[5]);
  and and_56 (and_56_out, ~FUNC_Code[0], FUNC_Code[1], ~FUNC_Code[2], ~FUNC_Code[3], ~FUNC_Code[4], ~FUNC_Code[5]);  // AND_Gate
  and and_57 (and_57_out, ~FUNC_Code[0], ~FUNC_Code[1], FUNC_Code[2], ~FUNC_Code[3], ~FUNC_Code[4], ~FUNC_Code[5]);  // AND_Gate
  and and_58 (and_58_out, FUNC_Code[0], ~FUNC_Code[1], ~FUNC_Code[2], ~FUNC_Code[3], ~FUNC_Code[4], ~FUNC_Code[5]);  // AND_Gate
  and and_59 (halt, and_55_out, OP_111111);
  and and_60 (rnd, and_56_out, OP_111111);
  and and_61 (kbd, and_57_out, OP_111111);
  and and_62 (tty, and_58_out, OP_111111);
  or or_10 (adds, add, RAM_OP, addi);
  or or_11 (subs, sub, B_Jump);
  or or_12 (ands, \and , andi);
  or or_13 (ors, \or , ori);
  or or_14 (xors, \xor , xori);
  or or_15 (slts, slt, sliti);
  or or_16 (sltus, sltu, slitiu);
  or or_17 (or_17_out, halt, 1'b1);
  Priority_Encoder priority_encoder_1 (
    .in0(1'b1), .in1(beq), .in2(bne), .in3(blez), .in4(bgtz), .in5(bltz), .in6(j), .in7(jr), .out(BC_Op),
    .en_in(1'b1));  // open: gs, en_out
  or or_18 (B_Jump, beq, bne, blez, bgtz, bltz);
  Priority_Encoder #(.select(2)) priority_encoder_2 (
    .in0(or_17_out), .in1(rnd), .in2(kbd), .in3(tty), .out(Special_Op), .en_in(1'b1));  // open: gs, en_out
  Priority_Encoder #(.disabled(0)) priority_encoder_3 (
    .in0(Branch_OP), .in1(ALU_OP_t), .in2(Immediate_OP), .in3(Register_OP), .in4(RAM_OP), .in5(Stack_OP),
    .in6(Special_OP_t), .out(CU_Op), .en_in(1'b1));  // open: in7, gs, en_out
  or or_19 (or_19_out, blez, bgtz, bltz);
  or or_20 (or_20_out, RAM_OP, Immediate_OP);
  or or_21 (or_21_out, lw, pop);
  and and_63 (and_63_out, ~B_Jump, ~RAM_OP, ~Immediate_OP, ~ALU_OP_t);  // AND_Gate
  or or_22 (rt_rd, OP_000000, OP_111000, OP_111111);
  Priority_Encoder #(.select(4)) priority_encoder_4 (
    .in0(adds), .in1(subs), .in2(ands), .in3(ors), .in4(\nor ), .in5(xors), .in6(slts), .in7(sltus),
    .in8(mult), .in9(mulu), .in10(div), .in11(divu), .in15(and_63_out), .out(ALU_Op), .en_in(1'b1));  // open: in12, in13, in14, gs, en_out
  Priority_Encoder #(.select(2)) priority_encoder_5 (
    .in0(1'b1), .in1(or_19_out), .in2(or_20_out), .out(B_Select), .en_in(1'b1));  // open: in3, gs, en_out
  Priority_Encoder priority_encoder_6 (
    .in0(1'b1), .in1(or_21_out), .in2(mfhi), .in3(mflo), .in4(kbd), .in5(rnd), .out(DI_Select));  // open: in6, in7, en_in, gs, en_out

  // Other names for the same wires on the sheet: Logical_Immediate_OP = Log_Imm_Op

  // Notes on the sheet:
  //   INPUTS
  //   No Op
  //   TIpo R
  //   Push/Pop
  //   Specials
  //   ALU 
  //   ALU 
  //   Op Code Decode
  //   Branch
  //   RAM
  //   Registers
  //   Func Code Decode
  //   Operations
  //   Stacks
  //   Specials
  //   Outputs
  //   CU
  //   BC
  //   ALU
  //   Specials
  //   Signals
endmodule

module RAM_Manager (
  input  [31:0] Address_In,
  input  Clk,
  input  Rst,
  input  Save_Data,
  input  [31:0] RAM_00,
  input  [31:0] RAM_01,
  input  [31:0] RAM_In,
  input  [31:0] RAM_02,
  input  [31:0] RAM_03,
  output [15:0] Address_Out,
  output [3:0] Mask,
  output [31:0] RAM_00_2,
  output [31:0] RAM_01_2,
  output [31:0] RAM_Out,
  output [31:0] RAM_02_2,
  output [31:0] RAM_03_2
);

  wire [1:0] Bank;
  wire [15:2] divider_1_rem;
  wire [31:0] shifter_1_out;

  Shifter #(.width(32), .shift("lr")) shifter_1 (.in(Address_In), .\dist (5'b00010), .out(shifter_1_out));
  Register #(.width(32)) register_1 (
    .D(RAM_In), .en(Save_Data), .Q({RAM_00_2[7:0], RAM_00_2[15:8], RAM_00_2[23:16], RAM_00_2[31:24]}),
    .clk(Clk), .clr(Rst));
  Decoder #(.select(2), .enable("false")) decoder_1 (
    .out0(Mask[0]), .out1(Mask[1]), .out2(Mask[2]), .out3(Mask[3]), .sel(Bank));
  Divider #(.width(16)) divider_1 (
    .a(shifter_1_out[15:0]), .b(16'h4), .out(Address_Out), .rem({divider_1_rem, Bank}));  // open: upper
  Multiplexer #(.select(2), .width(32), .enable("false")) multiplexer_1 (
    .in0(RAM_00), .in1(RAM_01), .in2(RAM_02), .in3(RAM_03),
    .out({RAM_Out[7:0], RAM_Out[15:8], RAM_Out[23:16], RAM_Out[31:24]}), .sel(Bank));

  assign RAM_01_2 = RAM_00_2;
  assign RAM_02_2 = RAM_00_2;
  assign RAM_03_2 = RAM_00_2;
endmodule

module Control_Unit (
  input  [5:0] Op_C,
  input  [3:0] Read_Time,
  input  [5:0] Func_C,
  input  [3:0] Write_Time,
  input  Clk,
  input  Rst,
  output [3:0] ALU_Op,
  output [2:0] Branch_Op,
  output Logical_Immediate_Op,
  output [2:0] DI_Select,
  output pop,
  output KBD_Enable,
  output TTY_Enable,
  output Chip_Selector,
  output RW_RAM,
  output Load_PC,
  output Load_Instruction,
  output R_W,
  output rt_rd,
  output [1:0] B_Selector,
  output [1:0] Select_Address,
  output Push,
  output Save_Data,
  output END
);

  wire and_1_out, CS_0, CS_1, CS_2, CS_3, CS_4, d_ff_1_q, d_ff_2_q, d_ff_7_q, demultiplexer_1_out0,
       demultiplexer_1_out1, demultiplexer_2_out0, demultiplexer_3_out0, demultiplexer_3_out4,
       demultiplexer_3_out5, demultiplexer_3_out6, demultiplexer_4_out1, demultiplexer_5_out1,
       demultiplexer_6_out0, demultiplexer_7_out0, demultiplexer_7_out1, demultiplexer_8_out0,
       demultiplexer_8_out1, demultiplexer_9_out0, demultiplexer_9_out1, demultiplexer_10_out0, Idle_q, lw,
       nor_1_out, not_1_out, or_4_out, or_5_out, or_7_out, or_8_out, pop_t, R_W_1, R_W_2, R_W_3, R_W_5,
       R_W_6, RAM_Op_1, RAM_Op_2, Stack_Op_1, Stack_Op_2, sw, Wait, WAIT_q;
  wire [1:0] S_Op;
  wire [2:0] CU_Op;
  wire [3:0] counter_1_q, RT____WT;

  Multiplexer #(.width(4), .enable("false")) multiplexer_1 (
    .in0(Read_Time), .in1(Write_Time), .out(RT____WT), .sel(RW_RAM));
  and and_1 (and_1_out, R_W_1, ~ALU_Op[3]);  // AND_Gate
  or or_1 (Chip_Selector, CS_0, CS_1, CS_2, CS_3, CS_4);
  or or_2 (R_W, and_1_out, R_W_2, R_W_3, CS_3, R_W_5, R_W_6, CS_2);
  Operation_Decoder operation_decoder_1 (
    .OP_Code(Op_C), .FUNC_Code(Func_C), .CU_Op(CU_Op), .BC_Op(Branch_Op), .ALU_Op(ALU_Op),
    .B_Select(B_Selector), .DI_Select(DI_Select), .Special_Op(S_Op), .Log_Imm_Op(Logical_Immediate_Op),
    .lw(lw), .pop(pop_t), .rt_rd(rt_rd));
  D_Flip_Flop d_ff_1 (.clk(Clk), .D(Chip_Selector), .Q(d_ff_1_q), .reset(Rst));  // open: Qn, preset, en
  Counter #(.width(4), .max('hf)) counter_1 (
    .load(Chip_Selector), .D(RT____WT), .count(d_ff_1_q), .Q(counter_1_q), .clk(Clk));  // open: carry, clr
  or or_3 (RW_RAM, CS_1, CS_4);
  or or_4 (or_4_out, RAM_Op_1, RAM_Op_2);
  or or_5 (or_5_out, Stack_Op_1, Stack_Op_2);
  Priority_Encoder #(.select(2)) priority_encoder_1 (
    .in0(1'b1), .in1(or_4_out), .in2(or_5_out), .out(Select_Address), .en_in(1'b1));  // open: in3, gs, en_out
  nor nor_1 (nor_1_out, counter_1_q[0], counter_1_q[1], counter_1_q[2], counter_1_q[3]);
  and and_2 (Wait, nor_1_out, d_ff_1_q);
  or or_6 (Save_Data, sw, Push);
  D_Flip_Flop Idle (.clk(Clk), .D(demultiplexer_1_out0), .Q(Idle_q), .preset(Rst));  // open: Qn, en, reset
  Demultiplexer #(.enable("false")) demultiplexer_1 (
    .out0(demultiplexer_1_out0), .out1(demultiplexer_1_out1), .in(Idle_q), .sel(not_1_out));
  not not_1 (not_1_out, Rst);
  or or_7 (or_7_out, demultiplexer_2_out0, d_ff_7_q, demultiplexer_1_out1);
  D_Flip_Flop Idle_2 (.clk(Clk), .D(or_7_out), .Q(CS_0), .reset(Rst));  // open: Qn, preset, en
  Demultiplexer #(.enable("false")) demultiplexer_2 (
    .out0(demultiplexer_2_out0), .out1(Load_Instruction), .in(CS_0), .sel(Wait));
  D_Flip_Flop d_ff_2 (.clk(Clk), .D(Load_Instruction), .Q(d_ff_2_q), .reset(Rst));  // open: Qn, preset, en
  Demultiplexer #(.select(3), .enable("false")) demultiplexer_3 (
    .out0(demultiplexer_3_out0), .out1(R_W_1), .out2(R_W_2), .out3(R_W_3), .out4(demultiplexer_3_out4),
    .out5(demultiplexer_3_out5), .out6(demultiplexer_3_out6), .in(d_ff_2_q), .sel(CU_Op));  // open: out7
  Demultiplexer #(.enable("false")) demultiplexer_4 (
    .out0(sw), .out1(demultiplexer_4_out1), .in(demultiplexer_3_out4), .sel(lw));
  Demultiplexer #(.enable("false")) demultiplexer_5 (
    .out0(Push), .out1(demultiplexer_5_out1), .in(demultiplexer_3_out5), .sel(pop_t));
  Demultiplexer #(.select(2), .enable("false")) demultiplexer_6 (
    .out0(demultiplexer_6_out0), .out1(R_W_6), .out2(R_W_5), .out3(TTY_Enable), .in(demultiplexer_3_out6),
    .sel(S_Op));
  or or_8 (or_8_out, END, demultiplexer_6_out0);
  or or_9 (Stack_Op_1, demultiplexer_9_out0, Push);
  or or_10 (Stack_Op_2, demultiplexer_10_out0, demultiplexer_5_out1);
  D_Flip_Flop u_END (.clk(Clk), .D(or_8_out), .Q(END), .en(demultiplexer_6_out0), .reset(Rst));  // open: Qn, preset
  or or_11 (RAM_Op_1, demultiplexer_7_out0, sw);
  or or_12 (RAM_Op_2, demultiplexer_8_out0, demultiplexer_4_out1);
  D_Flip_Flop d_ff_3 (.clk(Clk), .D(Stack_Op_1), .Q(CS_4), .reset(Rst));  // open: Qn, preset, en
  D_Flip_Flop d_ff_4 (.clk(Clk), .D(Stack_Op_2), .Q(CS_3), .reset(Rst));  // open: Qn, preset, en
  D_Flip_Flop d_ff_5 (.clk(Clk), .D(RAM_Op_1), .Q(CS_1), .reset(Rst));  // open: Qn, preset, en
  D_Flip_Flop d_ff_6 (.clk(Clk), .D(RAM_Op_2), .Q(CS_2), .reset(Rst));  // open: Qn, preset, en
  Demultiplexer #(.enable("false")) demultiplexer_7 (
    .out0(demultiplexer_7_out0), .out1(demultiplexer_7_out1), .in(CS_1), .sel(Wait));
  Demultiplexer #(.enable("false")) demultiplexer_8 (
    .out0(demultiplexer_8_out0), .out1(demultiplexer_8_out1), .in(CS_2), .sel(Wait));
  Demultiplexer #(.enable("false")) demultiplexer_9 (
    .out0(demultiplexer_9_out0), .out1(demultiplexer_9_out1), .in(CS_4), .sel(Wait));
  Demultiplexer #(.enable("false")) demultiplexer_10 (.out0(demultiplexer_10_out0), .out1(pop), .in(CS_3), .sel(Wait));
  D_Flip_Flop u_WAIT (.clk(Clk), .D(TTY_Enable), .Q(WAIT_q), .reset(Rst));  // open: Qn, preset, en
  D_Flip_Flop WAIT_2 (.clk(Clk), .D(R_W_5), .Q(KBD_Enable), .reset(Rst));  // open: Qn, preset, en
  or or_13 (Load_PC, demultiplexer_3_out0, R_W_1, R_W_2, R_W_3, demultiplexer_7_out1, demultiplexer_8_out1, demultiplexer_9_out1, pop, R_W_6, KBD_Enable, WAIT_q);
  D_Flip_Flop d_ff_7 (.clk(Clk), .D(Load_PC), .Q(d_ff_7_q), .reset(Rst));  // open: Qn, preset, en

  // Other names for the same wires on the sheet: Hi_Lo_Op = ALU_Op[3]; B_Select[1:0] = B_Selector;
  //   Bc_Op[2:0] = Branch_Op; CS = Chip_Selector; L_I_Op = Logical_Immediate_Op; Load_Inst = Load_Instruction;
  //   R_W_4 = CS_3; R_W_7 = CS_2; R_W_RAM_1 = CS_1; R_W_RAM_2 = CS_4; RT[3:0] = Read_Time; S_pop = pop;
  //   WT[3:0] = Write_Time

  // Notes on the sheet:
  //   OP-Dec
  //   Wait
  //   INPUTS
  //   Disjunction
  //   Branch Control OP
  //   ALU OP
  //   Immediate OP
  //   Register OP
  //   RAM OP
  //   Stack OP
  //   Special OP
  //   Store Word
  //   Load Word
  //   Push
  //   Pop
  //   OUTPUTS
endmodule

module Cache_Memory (
  input  [31:0] RAM_In_0,
  input  Clk,
  input  Rst,
  input  R_W,
  input  [31:0] RAM_In_1,
  input  Find,
  input  [3:0] RT,
  input  [31:0] RAM_In_2,
  input  [31:0] RAM_In_3,
  input  [31:0] Address,
  output [31:0] Instruction,
  output [15:0] RAM_Address,
  output [1:0] Offset,
  output HIT
);

  wire and_1_out, and_3_out, and_4_out, comparator_1_eq, comparator_2_eq, d_ff_1_q, En_0, En_1, En_2, En_3,
       nor_1_out, or_1_out, Ready_RT, V_0, V_1, V_2, V_3, Validated;
  wire [3:0] counter_1_q, subtractor_1_out;
  wire [13:0] Selected_Tag, Tag_0, Tag_1, Tag_3;
  wire [31:0] multiplexer_1_out, multiplexer_2_out, multiplexer_4_out, multiplexer_5_out, Out_0, Out_1,
       Out_2, Out_3, Out_4, Out_5, Out_6, Out_7, Out_8, Out_9, Out_10, Out_11, Out_12, Out_13, Out_14, Out_15;

  Register #(.width(14)) register_1 (.D(Address[19:6]), .en(En_0), .Q(Tag_0), .clk(Clk), .clr(Rst));
  Register #(.width(14)) register_2 (.D(Address[19:6]), .en(En_1), .Q(Tag_1), .clk(Clk), .clr(Rst));
  Register #(.width(14)) register_3 (.D(Address[19:6]), .en(En_2), .Q(Tag_1), .clk(Clk), .clr(Rst));
  Register #(.width(14)) register_4 (.D(Address[19:6]), .en(En_3), .Q(Tag_3), .clk(Clk), .clr(Rst));
  Multiplexer #(.select(2), .width(32), .enable("false")) multiplexer_1 (
    .in0(Out_0), .in1(Out_4), .in2(Out_8), .in3(Out_12), .out(multiplexer_1_out), .sel(Address[5:4]));
  Multiplexer #(.select(2), .width(32), .enable("false")) multiplexer_2 (
    .in0(Out_3), .in1(Out_7), .in2(Out_11), .in3(Out_15), .out(multiplexer_2_out), .sel(Address[5:4]));
  Multiplexer #(.select(2), .width(14), .enable("false")) multiplexer_3 (
    .in0(Tag_0), .in1(Tag_1), .in2(Tag_1), .in3(Tag_3), .out(Selected_Tag), .sel(Address[5:4]));
  Multiplexer #(.select(2), .width(32), .enable("false")) multiplexer_4 (
    .in0(Out_1), .in1(Out_5), .in2(Out_9), .in3(Out_13), .out(multiplexer_4_out), .sel(Address[5:4]));
  Multiplexer #(.select(2), .width(32), .enable("false")) multiplexer_5 (
    .in0(Out_2), .in1(Out_6), .in2(Out_10), .in3(Out_14), .out(multiplexer_5_out), .sel(Address[5:4]));
  Register #(.width(32)) register_5 (.D(RAM_In_0), .en(En_0), .Q(Out_0), .clk(Clk), .clr(Rst));
  Register #(.width(32)) register_6 (.D(RAM_In_0), .en(En_1), .Q(Out_4), .clk(Clk), .clr(Rst));
  Register #(.width(32)) register_7 (.D(RAM_In_0), .en(En_2), .Q(Out_8), .clk(Clk), .clr(Rst));
  Register #(.width(32)) register_8 (.D(RAM_In_0), .en(En_3), .Q(Out_12), .clk(Clk), .clr(Rst));
  Multiplexer #(.select(2), .enable("false")) multiplexer_6 (
    .in0(V_0), .in1(V_1), .in2(V_2), .in3(V_3), .out(Validated), .sel(Address[5:4]));
  Multiplexer #(.select(2), .width(32), .enable("false")) multiplexer_7 (
    .in0(multiplexer_1_out), .in1(multiplexer_4_out), .in2(multiplexer_5_out), .in3(multiplexer_2_out),
    .out({Instruction[7:0], Instruction[15:8], Instruction[23:16], Instruction[31:24]}), .sel(Address[3:2]));
  Register #(.width(32)) register_9 (.D(RAM_In_1), .en(En_0), .Q(Out_1), .clk(Clk), .clr(Rst));
  Register #(.width(32)) register_10 (.D(RAM_In_1), .en(En_1), .Q(Out_5), .clk(Clk), .clr(Rst));
  Register #(.width(32)) register_11 (.D(RAM_In_1), .en(En_2), .Q(Out_9), .clk(Clk), .clr(Rst));
  Register #(.width(32)) register_12 (.D(RAM_In_1), .en(En_3), .Q(Out_13), .clk(Clk), .clr(Rst));
  Register #(.width(32)) register_13 (.D(RAM_In_2), .en(En_0), .Q(Out_2), .clk(Clk), .clr(Rst));
  Register #(.width(32)) register_14 (.D(RAM_In_2), .en(En_1), .Q(Out_6), .clk(Clk), .clr(Rst));
  Register #(.width(32)) register_15 (.D(RAM_In_2), .en(En_2), .Q(Out_10), .clk(Clk), .clr(Rst));
  Register #(.width(32)) register_16 (.D(RAM_In_2), .en(En_3), .Q(Out_14), .clk(Clk), .clr(Rst));
  and and_1 (and_1_out, ~R_W, Find, ~HIT);  // AND_Gate
  Register #(.width(32)) register_17 (.D(RAM_In_3), .en(En_0), .Q(Out_3), .clk(Clk), .clr(Rst));
  Register #(.width(32)) register_18 (.D(RAM_In_3), .en(En_1), .Q(Out_7), .clk(Clk), .clr(Rst));
  Register #(.width(32)) register_19 (.D(RAM_In_3), .en(En_2), .Q(Out_11), .clk(Clk), .clr(Rst));
  Register #(.width(32)) register_20 (.D(RAM_In_3), .en(En_3), .Q(Out_15), .clk(Clk), .clr(Rst));
  Comparator #(.width(14)) comparator_1 (.a(Selected_Tag), .b(Address[19:6]), .eq(comparator_1_eq));  // open: gt, lt
  and and_2 (HIT, comparator_1_eq, Ready_RT);
  and and_3 (and_3_out, and_1_out, ~Ready_RT);  // AND_Gate
  Subtractor #(.width(4)) subtractor_1 (.a(RT), .b(4'b0001), .out(subtractor_1_out));  // open: bin, bout
  D_Flip_Flop d_ff_1 (.clk(Clk), .D(and_3_out), .Q(d_ff_1_q), .reset(Rst));  // open: Qn, preset, en
  Counter #(.width(4), .max('hf)) counter_1 (
    .load(and_1_out), .D(subtractor_1_out), .count(d_ff_1_q), .Q(counter_1_q), .clk(Clk), .clr(Rst));  // open: carry
  D_Flip_Flop d_ff_2 (.clk(Clk), .D(Ready_RT), .Q(V_0), .en(En_0), .reset(Rst));  // open: Qn, preset
  D_Flip_Flop d_ff_3 (.clk(Clk), .D(Ready_RT), .Q(V_1), .en(En_1), .reset(Rst));  // open: Qn, preset
  D_Flip_Flop d_ff_4 (.clk(Clk), .D(Ready_RT), .Q(V_2), .en(En_2), .reset(Rst));  // open: Qn, preset
  D_Flip_Flop d_ff_5 (.clk(Clk), .D(Ready_RT), .Q(V_3), .en(En_3), .reset(Rst));  // open: Qn, preset
  or or_1 (or_1_out, Ready_RT, R_W);
  Demultiplexer #(.select(2), .enable("false")) demultiplexer_1 (
    .out0(En_0), .out1(En_1), .out2(En_2), .out3(En_3), .in(or_1_out), .sel(Address[5:4]));
  nor nor_1 (nor_1_out, counter_1_q[0], counter_1_q[1], counter_1_q[2], counter_1_q[3]);
  and and_4 (and_4_out, nor_1_out, d_ff_1_q);
  Comparator #(.width(4)) comparator_2 (.a(RT), .b(4'b0000), .eq(comparator_2_eq));  // open: gt, lt
  or or_2 (Ready_RT, and_4_out, comparator_2_eq);

  assign Offset = Address[3:2];
  assign RAM_Address = Address[19:4];

  // Other names for the same wires on the sheet: Index[1:0] = Address[5:4]; R_Address[15:0] = Address[19:4];
  //   Tag[13:0] = Address[19:6]; In_0[31:0] = RAM_In_0; In_1[31:0] = RAM_In_1; In_2[31:0] = RAM_In_2;
  //   In_3[31:0] = RAM_In_3; Tag_2[13:0] = Tag_1; Validate = Ready_RT

  // Notes on the sheet:
  //   Inputs
  //   Tags
  //   Search Process
  //   Set Instruction
  //   Memory
  //   Validate
  //   RT Waiting Process
  //   Outputs
endmodule
